// Logisim project LAB 4. BCD to Excess 3.circ as structural Verilog: 1 circuit, main circuit main
module main (
  input  A,
  input  B,
  input  C,
  input  D,
  output W,
  output X,
  output Y,
  output Z
);

  wire nand_1_out, nand_2_out, nand_3_out, nand_4_out, nand_5_out, nand_6_out, nand_7_out, nand_9_out,
       nand_10_out, nand_11_out, nand_12_out;

  nand nand_1 (nand_1_out, B, D);
  nand nand_2 (nand_2_out, B, A);
  nand nand_3 (nand_3_out, A, A);
  nand nand_4 (nand_4_out, B, B);
  nand nand_5 (nand_5_out, A, A);
  nand nand_6 (nand_6_out, D, D);
  nand nand_7 (nand_7_out, A, D);
  nand nand_8 (Z, D, D);
  nand nand_9 (nand_9_out, D, nand_4_out);
  nand nand_10 (nand_10_out, nand_4_out, A);
  nand nand_11 (nand_11_out, B, nand_5_out, nand_6_out);
  nand nand_12 (nand_12_out, nand_6_out, nand_5_out);
  nand nand_13 (W, nand_1_out, nand_2_out, nand_3_out);
  nand nand_14 (X, nand_9_out, nand_10_out, nand_11_out);
  nand nand_15 (Y, nand_12_out, nand_7_out);

  assign C = A;

  // Notes on the sheet:
  //   Mohammed Mahmudur Rahman
  //   Student ID# 1520386043
endmodule
