// Logisim project LAB 6. 7 segment display. basic gates.circ as structural Verilog: 1 circuit, main circuit main
module main (
  input  A,
  input  B,
  input  C,
  input  D
);

  wire and_1_out, and_2_out, and_3_out, and_4_out, and_5_out, and_6_out, and_7_out, and_8_out, and_9_out,
       and_10_out, not_1_out, not_2_out, not_3_out, not_4_out, or_1_out, or_2_out, or_3_out, or_4_out,
       or_5_out, or_6_out, or_7_out;

  not not_1 (not_1_out, A);
  not not_2 (not_2_out, B);
  not not_3 (not_3_out, D);
  not not_4 (not_4_out, C);
  and and_1 (and_1_out, B, D);
  and and_2 (and_2_out, not_2_out, not_3_out);
  and and_3 (and_3_out, not_4_out, not_3_out);
  and and_4 (and_4_out, C, D);
  and and_5 (and_5_out, C, not_3_out);
  and and_6 (and_6_out, not_2_out, C);
  and and_7 (and_7_out, B, not_4_out, D);
  and and_8 (and_8_out, B, not_4_out);
  and and_9 (and_9_out, not_3_out, B);
  and and_10 (and_10_out, C, D, not_2_out);
  or or_1 (or_1_out, and_1_out, and_2_out, C, A);
  or or_2 (or_2_out, and_3_out, and_4_out, not_2_out);
  or or_3 (or_3_out, not_4_out, D, B);
  or or_4 (or_4_out, and_2_out, and_5_out, and_6_out, and_7_out, A);
  or or_5 (or_5_out, and_5_out, and_2_out);
  or or_6 (or_6_out, and_8_out, and_9_out, A, and_3_out);
  or or_7 (or_7_out, and_8_out, and_5_out, A, and_10_out);
  _7_Segment_Display u_7_segment_display_1 (
    .g(or_7_out), .f(or_6_out), .a(or_1_out), .b(or_2_out), .e(or_5_out), .d(or_4_out), .c(or_3_out));  // open: dp

  // Notes on the sheet:
  //   Mohammed Mahmudur Rahman
  //   ID# 1520386043
  //   f
  //   g
  //   a
  //   b
  //   c
  //   d
  //   e
endmodule
