// Logisim project LAB 6. 7 segment display. decoder.circ as structural Verilog: 1 circuit, main circuit main
module main (
  input  [3:0] in_1
);

  wire decoder_1_out0, decoder_1_out1, decoder_1_out2, decoder_1_out3, decoder_1_out4, decoder_1_out5,
       decoder_1_out6, decoder_1_out7, decoder_1_out8, decoder_1_out9;

  Decoder #(.select(4)) decoder_1 (
    .out0(decoder_1_out0), .out1(decoder_1_out1), .out2(decoder_1_out2), .out3(decoder_1_out3),
    .out4(decoder_1_out4), .out5(decoder_1_out5), .out6(decoder_1_out6), .out7(decoder_1_out7),
    .out8(decoder_1_out8), .out9(decoder_1_out9), .sel(in_1));  // open: out10, out11, out12, out13, out14, out15, en
  _7_Segment_Display u_7_segment_display_1 (.b(decoder_1_out1), .c(decoder_1_out1));  // open: g, f, a, e, d, dp
  _7_Segment_Display u_7_segment_display_2 (
    .f(decoder_1_out0), .a(decoder_1_out0), .b(decoder_1_out0), .e(decoder_1_out0), .d(decoder_1_out0),
    .c(decoder_1_out0), .dp(decoder_1_out0));  // open: g
  _7_Segment_Display u_7_segment_display_3 (
    .g(decoder_1_out4), .f(decoder_1_out4), .b(decoder_1_out4), .c(decoder_1_out4));  // open: a, e, d, dp
  _7_Segment_Display u_7_segment_display_4 (
    .g(decoder_1_out5), .f(decoder_1_out5), .a(decoder_1_out5), .d(decoder_1_out5), .c(decoder_1_out5));  // open: b, e, dp
  _7_Segment_Display u_7_segment_display_5 (
    .g(decoder_1_out8), .f(decoder_1_out8), .a(decoder_1_out8), .b(decoder_1_out8), .e(decoder_1_out8),
    .d(decoder_1_out8), .c(decoder_1_out8));  // open: dp
  _7_Segment_Display u_7_segment_display_6 (
    .g(decoder_1_out9), .f(decoder_1_out9), .a(decoder_1_out9), .b(decoder_1_out9), .c(decoder_1_out9));  // open: e, d, dp
  _7_Segment_Display u_7_segment_display_7 (
    .g(decoder_1_out2), .a(decoder_1_out2), .b(decoder_1_out2), .e(decoder_1_out2), .d(decoder_1_out2));  // open: f, c, dp
  _7_Segment_Display u_7_segment_display_8 (
    .g(decoder_1_out6), .f(decoder_1_out6), .a(decoder_1_out6), .e(decoder_1_out6), .d(decoder_1_out6),
    .c(decoder_1_out6));  // open: b, dp
  _7_Segment_Display u_7_segment_display_9 (
    .g(decoder_1_out3), .a(decoder_1_out3), .b(decoder_1_out3), .d(decoder_1_out3), .c(decoder_1_out3));  // open: f, e, dp
  _7_Segment_Display u_7_segment_display_10 (
    .a(decoder_1_out7), .b(decoder_1_out7), .c(decoder_1_out7));  // open: g, f, e, d, dp

  // Notes on the sheet:
  //   Mohammed Mahmudur Rahman
  //   ID# 1520386043
endmodule
