// Logisim project LAB 8.circ as structural Verilog: 1 circuit, main circuit main
module main (
  input  in_1
);

  wire and_1_out, clock_1_out, t_ff_2_q, t_ff_3_q;

  and and_1 (and_1_out, t_ff_3_q, t_ff_2_q);
  Clock clock_1 (.out(clock_1_out));
  T_Flip_Flop #(.trigger("falling")) t_ff_1 (.clk(clock_1_out), .T(and_1_out));  // open: Q, Qn, preset, reset, en
  T_Flip_Flop #(.trigger("falling")) t_ff_2 (
    .clk(clock_1_out), .T(t_ff_3_q), .Q(t_ff_2_q));  // open: Qn, preset, reset, en
  T_Flip_Flop #(.trigger("falling")) t_ff_3 (.clk(clock_1_out), .T(in_1), .Q(t_ff_3_q));  // open: Qn, preset, reset, en
endmodule
