// Logisim project Lab 5.circ as structural Verilog: 1 circuit, main circuit main
module main (
  input  in_1,
  input  in_2,
  input  in_3,
  input  in_4,
  input  in_5,
  input  in_6,
  input  in_7,
  input  in_8,
  input  in_9,
  output out_10,
  output out_11,
  output out_12,
  output out_13,
  output out_14,
  output out_15,
  output out_16,
  output out_17
);

  wire xor_1_out, xor_2_out, xor_3_out, xor_4_out;

  Adder #(.width(1)) adder_1 (.a(in_1), .b(xor_1_out), .out(out_10), .cin(in_5), .cout(out_14));
  xor xor_1 (xor_1_out, in_8, in_5);
  xor xor_2 (xor_2_out, in_9, in_5);
  Adder #(.width(1)) adder_2 (.a(in_2), .b(xor_2_out), .out(out_11), .cin(in_5), .cout(out_17));
  xor xor_3 (xor_3_out, in_7, in_5);
  Adder #(.width(1)) adder_3 (.a(in_3), .b(xor_3_out), .out(out_12), .cin(in_5), .cout(out_15));
  Adder #(.width(1)) adder_4 (.a(in_4), .b(xor_4_out), .out(out_13), .cin(in_5), .cout(out_16));
  xor xor_4 (xor_4_out, in_6, in_5);

  // Notes on the sheet:
  //   Mohammed Mahmudur Rahman
  //   Student ID# 1520386043
endmodule
