// Logisim project lab 1.circ as structural Verilog: 1 circuit, main circuit main
module main (
  input  A,
  input  B,
  input  C,
  output out_4
);

  wire and_1_out, and_2_out, and_3_out, not_1_out, not_2_out, or_1_out;

  not not_1 (not_1_out, A);
  not not_2 (not_2_out, C);
  and and_1 (and_1_out, A, B);
  and and_2 (and_2_out, B, C);
  and and_3 (and_3_out, not_1_out, not_2_out);
  or or_1 (or_1_out, and_1_out, and_2_out);
  or or_2 (out_4, or_1_out, and_3_out);

  // Notes on the sheet:
  //   A'
  //   C'
  //   AB
  //   BC
  //   A'C'
  //   Mohammed Mahmudur Rahman
  //   Student ID# 1520386043
  //   (AB+BC)
  //   F=AB+BC+A'C'
endmodule
