// Logisim project lab 7. mux internal.circ as structural Verilog: 1 circuit, main circuit main
module main (
  input  I_0,
  input  I_1,
  input  I__3,
  input  S_1,
  input  S_0,
  output out_6
);

  wire and_1_out, and_2_out, and_3_out, and_4_out, not_1_out, not_2_out, or_1_out, or_2_out;

  not not_1 (not_1_out, S_1);
  not not_2 (not_2_out, S_0);
  and and_1 (and_1_out, I_0, not_1_out, not_2_out);
  and and_2 (and_2_out, I_1, not_1_out, S_0);
  and and_3 (and_3_out, I__3, S_1, not_2_out);
  and and_4 (and_4_out, I__3, S_1, S_0);
  or or_1 (or_1_out, and_1_out, and_2_out);
  or or_2 (or_2_out, and_3_out, and_4_out);
  or or_3 (out_6, or_1_out, or_2_out);

  // Notes on the sheet:
  //   I. 2
  //   Mohammed Mahmudur Rahman
  //   Mux Internal Circuit
  //   ID# 1520386043
endmodule
