// Logisim project lab 7. mux.circ as structural Verilog: 1 circuit, main circuit main
module main (
  input  in_1,
  input  in_2,
  input  in_3,
  input  [1:0] in_4,
  output out_5
);

  Multiplexer #(.select(2)) multiplexer_1 (
    .in0(in_1), .in1(in_2), .in2(in_3), .in3(in_3), .out(out_5), .sel(in_4));  // open: en

  // Notes on the sheet:
  //   Mohammed Mahmudur Rahman
  //   Student ID# 1520386043
  //   Logisim 2
endmodule
