// Logisim project lab 7.8x1  mux.circ as structural Verilog: 1 circuit, main circuit main
module main (
  input  in_1,
  input  in_2,
  input  in_3,
  input  in_4,
  input  [2:0] in_5,
  input  in_6,
  output out_7
);

  wire not_1_out;

  not not_1 (not_1_out, in_6);
  Multiplexer #(.select(3)) multiplexer_1 (
    .in0(in_6), .in1(not_1_out), .in2(in_1), .in3(in_2), .in4(in_2), .in5(not_1_out), .in6(in_3), .in7(in_4),
    .out(out_7), .sel(in_5));  // open: en

  // Notes on the sheet:
  //   Mohammed Mahmudur Rahman
  //   ID# 15250386043
endmodule
