// Logisim project lab final sequential.circ as structural Verilog: 1 circuit, main circuit main
module main (
  input  W,
  input  X,
  input  Y,
  input  Z,
  input  in_5,
  output A,
  output B,
  output C,
  output D,
  output out_10,
  output out_11,
  output out_12,
  output out_13
);

  wire and_1_out, and_2_out, and_3_out, and_4_out, and_5_out, and_6_out, and_7_out, and_8_out, and_9_out,
       clock_1_out, not_1_out, not_2_out, not_3_out, not_4_out, not_5_out, not_6_out;

  Clock clock_1 (.out(clock_1_out));
  and and_1 (and_1_out, out_12, out_11);
  not not_1 (not_1_out, out_10);
  not not_2 (not_2_out, out_12);
  not not_3 (not_3_out, out_10);
  not not_4 (not_4_out, out_11);
  not not_5 (not_5_out, out_12);
  not not_6 (not_6_out, out_11);
  not not_7 (D, out_11);
  or or_1 (A, and_1_out, out_10, out_13);
  and and_2 (and_2_out, not_1_out, not_2_out);
  and and_3 (and_3_out, not_3_out, not_4_out);
  and and_4 (and_4_out, out_10, out_12, out_11);
  and and_5 (and_5_out, not_5_out, out_11);
  and and_6 (and_6_out, out_12, not_6_out);
  T_Flip_Flop t_ff_1 (.clk(clock_1_out), .T(in_5), .Q(out_11));  // open: Qn, preset, reset, en
  or or_2 (B, and_2_out, and_3_out, and_4_out);
  or or_3 (C, and_5_out, and_6_out);
  and and_7 (and_7_out, in_5, out_11);
  T_Flip_Flop t_ff_2 (.clk(clock_1_out), .T(and_7_out), .Q(out_12));  // open: Qn, preset, reset, en
  and and_8 (and_8_out, and_7_out, out_12);
  T_Flip_Flop t_ff_3 (.clk(clock_1_out), .T(and_8_out), .Q(out_10));  // open: Qn, preset, reset, en
  and and_9 (and_9_out, and_8_out, out_10);
  T_Flip_Flop t_ff_4 (.clk(clock_1_out), .T(and_9_out), .Q(out_13));  // open: Qn, preset, reset, en

  // Other names for the same wires on the sheet: W_t = out_13; X_t = out_10; Y_t = out_12; Z_t = out_11

  // Notes on the sheet:
  //   1520386043
  //   Mohammed mahmudur rahman
endmodule
