// Logisim project EEE211. project-decoder. Mohammed Mahmudur Rahman. 1520386043 .circ as structural Verilog: 1 circuit, main circuit main
module main (
  input  in_1,
  input  in_2,
  output Z,
  output Y,
  output X
);

  wire _0, _1, _2, _3, _4, _5, _6, _7, a, and_1_out, and_2_out, c, clock_1_out, d, e, f, g;

  Clock clock_1 (.out(clock_1_out));
  and and_1 (and_1_out, in_2, clock_1_out);
  and and_2 (and_2_out, Y, Z);
  Decoder #(.select(3)) decoder_1 (
    .out0(_0), .out1(_1), .out2(_2), .out3(_3), .out4(_4), .out5(_5), .out6(_6), .out7(_7), .sel({X, Y, Z}));  // open: en
  J_K_Flip_Flop j_k_ff_1 (.J(in_1), .clk(and_1_out), .K(in_1), .Q(Z));  // open: Qn, preset, en, reset
  J_K_Flip_Flop j_k_ff_2 (.J(Z), .clk(and_1_out), .K(Z), .Q(Y));  // open: Qn, preset, en, reset
  J_K_Flip_Flop j_k_ff_3 (.J(and_2_out), .clk(and_1_out), .K(and_2_out), .Q(X));  // open: Qn, preset, en, reset
  _7_Segment_Display u_7_segment_display_1 (.g(g), .f(f), .a(a), .b(_5), .e(e), .d(d), .c(c));  // open: dp
  or u_f (f, _0, _1, _3, _4, _5, _6);
  or or_1 (d, _1, _3, _4, _5, _6);
  or or_2 (g, _0, _1, _2, _4, _6);
  or u_a (a, _0, _1, _3, _4, _5, _6);
  or u_e (e, _0, _1, _2, _3, _4, _5);
  or or_3 (c, _2, _5, _6);

  // Other names for the same wires on the sheet: b = _5

  // Notes on the sheet:
  //   Y
  //   X
  //   Z
  //   Mohammed Mahmudur Rahman
  //   Student ID# 1520386043
endmodule
