// Logisim project Md-Sharuar-zahan-rejon.circ as structural Verilog: 1 circuit, main circuit main
module main (
  input  in_1,
  input  in_2,
  output a,
  output Z,
  output Y,
  output b,
  output X,
  output c,
  output f,
  output d,
  output g,
  output e
);

  wire and_1_out, and_2_out, clock_1_out, nand_1_out, nand_2_out, nand_3_out, nand_4_out, nand_5_out,
       nand_6_out, nand_7_out, nand_8_out, nand_10_out, nand_11_out, nand_12_out, nand_13_out, nand_14_out,
       nand_15_out, nand_16_out, nand_17_out, nand_22_out, nand_23_out, nand_24_out, nand_25_out,
       nand_26_out, nand_27_out, nand_28_out;

  Clock clock_1 (.out(clock_1_out));
  and and_1 (and_1_out, in_2, clock_1_out);
  and and_2 (and_2_out, Y, Z);
  J_K_Flip_Flop j_k_ff_1 (.J(in_1), .clk(and_1_out), .K(in_1), .Q(Z));  // open: Qn, preset, en, reset
  J_K_Flip_Flop j_k_ff_2 (.J(Z), .clk(and_1_out), .K(Z), .Q(Y));  // open: Qn, preset, en, reset
  J_K_Flip_Flop j_k_ff_3 (.J(and_2_out), .clk(and_1_out), .K(and_2_out), .Q(X));  // open: Qn, preset, en, reset
  nand nand_1 (nand_1_out, X, X);
  nand nand_2 (nand_2_out, Z, Z);
  nand nand_3 (nand_3_out, Y, Y);
  nand nand_4 (nand_4_out, Z, Z);
  nand nand_5 (nand_5_out, Y, Y);
  nand nand_6 (nand_6_out, X, X);
  nand nand_7 (nand_7_out, Y, Y);
  nand nand_8 (nand_8_out, Z, Z);
  nand nand_9 (e, X, Y);
  nand nand_10 (nand_10_out, nand_1_out, Z);
  nand nand_11 (nand_11_out, X, nand_2_out);
  nand nand_12 (nand_12_out, X, nand_3_out, Z);
  nand nand_13 (nand_13_out, Y, nand_4_out);
  nand nand_14 (nand_14_out, X, nand_5_out, Z);
  nand nand_15 (nand_15_out, nand_6_out, Z);
  nand nand_16 (nand_16_out, X, nand_7_out);
  nand nand_17 (nand_17_out, X, nand_8_out);
  nand nand_18 (a, Y, nand_10_out, nand_11_out);
  nand nand_19 (b, nand_12_out, nand_12_out);
  nand nand_20 (c, nand_13_out, nand_14_out);
  nand nand_21 (d, nand_15_out, nand_16_out, nand_17_out);
  _7_Segment_Display u_7_segment_display_1 (.g(g), .f(f), .a(a), .b(b), .e(e), .d(d), .c(c));  // open: dp
  nand nand_22 (nand_22_out, X, X);
  nand nand_23 (nand_23_out, Z, Z);
  nand nand_24 (nand_24_out, X, X);
  nand nand_25 (nand_25_out, Y, Y);
  nand nand_26 (nand_26_out, nand_22_out, Z);
  nand nand_27 (nand_27_out, X, nand_23_out);
  nand nand_28 (nand_28_out, nand_24_out, nand_25_out);
  nand nand_29 (f, Y, nand_26_out, nand_27_out);
  nand nand_30 (g, nand_28_out, Z);

  // Notes on the sheet:
  //   ID:
  //   Md.Sharuar Zahan Rejon
  //   1431048043
endmodule
