// Logisim project Project211.circ as structural Verilog: 1 circuit, main circuit main
module main (
  input  in_1,
  input  X,
  input  in_3,
  input  Y,
  input  Z,
  output a,
  output Z_2,
  output Y_2,
  output b,
  output X_2,
  output c,
  output f,
  output d,
  output g,
  output e
);

  wire and_1_out, and_2_out, clock_1_out, nand_1_out, nand_2_out, nand_3_out, nand_4_out, nand_5_out,
       nand_6_out, nand_7_out, nand_8_out, nand_10_out, nand_11_out, nand_12_out, nand_13_out, nand_14_out,
       nand_15_out, nand_16_out, nand_17_out, nand_22_out, nand_23_out, nand_24_out, nand_25_out,
       nand_26_out, nand_27_out, nand_28_out;

  Clock clock_1 (.out(clock_1_out));
  and and_1 (and_1_out, in_3, clock_1_out);
  and and_2 (and_2_out, Y_2, Z_2);
  J_K_Flip_Flop j_k_ff_1 (.J(in_1), .clk(and_1_out), .K(in_1), .Q(Z_2));  // open: Qn, preset, en, reset
  J_K_Flip_Flop j_k_ff_2 (.J(Z_2), .clk(and_1_out), .K(Z_2), .Q(Y_2));  // open: Qn, preset, en, reset
  J_K_Flip_Flop j_k_ff_3 (.J(and_2_out), .clk(and_1_out), .K(and_2_out), .Q(X_2));  // open: Qn, preset, en, reset
  nand nand_1 (nand_1_out, X_2, X_2);
  nand nand_2 (nand_2_out, Z_2, Z_2);
  nand nand_3 (nand_3_out, Y_2, Y_2);
  nand nand_4 (nand_4_out, Z_2, Z_2);
  nand nand_5 (nand_5_out, Y_2, Y_2);
  nand nand_6 (nand_6_out, X_2, X_2);
  nand nand_7 (nand_7_out, Y_2, Y_2);
  nand nand_8 (nand_8_out, Z_2, Z_2);
  nand nand_9 (e, X_2, Y_2);
  nand nand_10 (nand_10_out, nand_1_out, Z_2);
  nand nand_11 (nand_11_out, X_2, nand_2_out);
  nand nand_12 (nand_12_out, X_2, nand_3_out, Z_2);
  nand nand_13 (nand_13_out, Y_2, nand_4_out);
  nand nand_14 (nand_14_out, X_2, nand_5_out, Z_2);
  nand nand_15 (nand_15_out, nand_6_out, Z_2);
  nand nand_16 (nand_16_out, X_2, nand_7_out);
  nand nand_17 (nand_17_out, X_2, nand_8_out);
  nand nand_18 (a, Y_2, nand_10_out, nand_11_out);
  nand nand_19 (b, nand_12_out, nand_12_out);
  nand nand_20 (c, nand_13_out, nand_14_out);
  nand nand_21 (d, nand_15_out, nand_16_out, nand_17_out);
  _7_Segment_Display u_7_segment_display_1 (.g(g), .f(f), .a(a), .b(b), .e(e), .d(d), .c(c));  // open: dp
  nand nand_22 (nand_22_out, X_2, X_2);
  nand nand_23 (nand_23_out, Z_2, Z_2);
  nand nand_24 (nand_24_out, X_2, X_2);
  nand nand_25 (nand_25_out, Y_2, Y_2);
  nand nand_26 (nand_26_out, nand_22_out, Z_2);
  nand nand_27 (nand_27_out, X_2, nand_23_out);
  nand nand_28 (nand_28_out, nand_24_out, nand_25_out);
  nand nand_29 (f, Y_2, nand_26_out, nand_27_out);
  nand nand_30 (g, nand_28_out, Z_2);

  // Other names for the same wires on the sheet: X_t = X_2; Y_t = Y_2; Z_t = Z_2
endmodule
