// Logisim project LogisimOfBABAFAFA_using_SEQUENTIAL_CIRCUIT.circ as structural Verilog: 1 circuit, main circuit main
module main (
  input  in_1,
  input  in_2
);

  wire and_1_out, button_1_out, clock_1_out, j_k_ff_1_q, j_k_ff_1_qn, j_k_ff_2_q, j_k_ff_2_qn, j_k_ff_3_q,
       not_1_out, not_2_out, or_1_out, or_2_out, or_3_out, or_4_out, or_5_out, or_6_out;

  Button button_1 (.out(button_1_out));
  Clock clock_1 (.out(clock_1_out));
  J_K_Flip_Flop j_k_ff_1 (
    .J(in_1), .clk(clock_1_out), .K(in_1), .Q(j_k_ff_1_q), .Qn(j_k_ff_1_qn), .reset(button_1_out));  // open: preset, en
  J_K_Flip_Flop j_k_ff_2 (
    .J(j_k_ff_1_q), .clk(clock_1_out), .K(j_k_ff_1_q), .Q(j_k_ff_2_q), .Qn(j_k_ff_2_qn), .reset(button_1_out));  // open: preset, en
  and and_1 (and_1_out, j_k_ff_1_q, j_k_ff_2_q);
  J_K_Flip_Flop j_k_ff_3 (
    .J(and_1_out), .clk(clock_1_out), .K(and_1_out), .Q(j_k_ff_3_q), .reset(button_1_out));  // open: Qn, preset, en
  not not_1 (not_1_out, j_k_ff_3_q);
  not not_2 (not_2_out, j_k_ff_2_q);
  or or_1 (or_1_out, not_1_out, not_2_out);
  or or_2 (or_2_out, not_1_out, not_2_out);
  or or_3 (or_3_out, j_k_ff_3_q, not_1_out);
  or or_4 (or_4_out, j_k_ff_3_q, not_1_out);
  or or_5 (or_5_out, j_k_ff_3_q, not_1_out);
  or or_6 (or_6_out, j_k_ff_3_q, not_1_out);
  _7_Segment_Display u_7_segment_display_1 (
    .g(or_6_out), .f(or_4_out), .a(or_5_out), .b(or_1_out), .e(or_3_out), .d(not_1_out), .c(or_2_out),
    .dp(in_2));

  // Notes on the sheet:
  //   a
  //   c
  //   d
  //   b
  //   e
  //   f
  //   g
endmodule
