// Logisim project Week 2 task 3 (Using NOR).circ as structural Verilog: 2 circuits, main circuit main
module main (
  input  A,
  input  B,
  input  C,
  output AC__BC_prime
);

  wire n7402_1_out_9, n7402_1_out_10, n7402_1_out_11, n7402_1_out_12, n7402_2_out_9, n7402_2_out_11;

  _7402 u_7402_1 (
    .in_1(C), .in_2(C), .in_3(A), .in_4(A), .in_5(n7402_1_out_9), .in_6(n7402_1_out_10), .in_7(B), .in_8(B),
    .out_9(n7402_1_out_9), .out_10(n7402_1_out_10), .out_11(n7402_1_out_11), .out_12(n7402_1_out_12));
  _7402 u_7402_2 (
    .in_1(n7402_1_out_12), .in_2(C), .in_5(n7402_2_out_9), .in_6(n7402_1_out_11), .in_7(n7402_2_out_11),
    .in_8(n7402_2_out_11), .out_9(n7402_2_out_9), .out_11(n7402_2_out_11), .out_12(AC__BC_prime));  // open: in_3, in_4, out_10

  // Notes on the sheet:
  //   A'
  //   C'
  //   B'
  //   AC
  //   BC'
  //   (AC + BC' )'
endmodule

module _7402 (
  input  in_1,
  input  in_2,
  input  in_3,
  input  in_4,
  input  in_5,
  input  in_6,
  input  in_7,
  input  in_8,
  output out_9,
  output out_10,
  output out_11,
  output out_12
);

  nor nor_1 (out_9, in_1, in_2);
  nor nor_2 (out_10, in_3, in_4);
  nor nor_3 (out_11, in_5, in_6);
  nor nor_4 (out_12, in_7, in_8);
endmodule
