// Logisim project Maxterm.circ as structural Verilog: 4 circuits, main circuit main
module main (
  input  S1,
  input  S2,
  input  C1,
  input  C2,
  output out_5
);

  wire n7404_1_out_7, n7404_1_out_8, n7404_1_out_9, n7404_1_out_10, n7408_1_out_9, n7408_1_out_10,
       n7408_1_out_11, n7408_1_out_12, n7408_2_out_9, n7408_2_out_10, n7408_2_out_12, n7408_3_out_9,
       n7408_3_out_10, n7432_1_out_9, n7432_1_out_10, n7432_1_out_11, n7432_1_out_12, n7432_2_out_9,
       n7432_2_out_10, n7432_2_out_11, n7432_2_out_12, n7432_3_out_9, n7432_3_out_10, n7432_3_out_11,
       n7432_3_out_12, n7432_4_out_9, n7432_4_out_10, n7432_4_out_11, n7432_4_out_12, n7432_5_out_9,
       n7432_5_out_10, n7432_5_out_11, n7432_5_out_12, n7432_6_out_9, n7432_6_out_10, n7432_6_out_12,
       n7432_7_out_9, n7432_7_out_10, n7432_7_out_12;

  _7404 u_7404_1 (
    .in_1(C1), .in_2(S2), .in_3(S1), .in_4(C2), .out_7(n7404_1_out_7), .out_8(n7404_1_out_8),
    .out_9(n7404_1_out_9), .out_10(n7404_1_out_10));  // open: in_5, in_6, out_11, out_12
  _7432 u_7432_1 (
    .in_1(C2), .in_2(C1), .in_3(S2), .in_4(S1), .in_5(n7432_3_out_9), .in_6(n7432_1_out_10),
    .in_7(n7432_1_out_9), .in_8(n7432_1_out_10), .out_9(n7432_1_out_9), .out_10(n7432_1_out_10),
    .out_11(n7432_1_out_11), .out_12(n7432_1_out_12));
  _7432 u_7432_2 (
    .in_1(n7432_2_out_10), .in_2(n7432_1_out_10), .in_3(C1), .in_4(n7404_1_out_10), .in_5(C2),
    .in_6(n7404_1_out_7), .in_7(n7432_2_out_11), .in_8(n7432_1_out_10), .out_9(n7432_2_out_9),
    .out_10(n7432_2_out_10), .out_11(n7432_2_out_11), .out_12(n7432_2_out_12));
  _7432 u_7432_3 (
    .in_1(n7404_1_out_10), .in_2(n7404_1_out_7), .in_3(n7404_1_out_8), .in_4(S1), .in_5(n7432_3_out_10),
    .in_6(n7432_3_out_12), .in_7(n7404_1_out_10), .in_8(C1), .out_9(n7432_3_out_9), .out_10(n7432_3_out_10),
    .out_11(n7432_3_out_11), .out_12(n7432_3_out_12));
  _7432 u_7432_4 (
    .in_1(n7432_4_out_10), .in_2(n7432_3_out_10), .in_3(C2), .in_4(n7404_1_out_7), .in_5(n7432_3_out_10),
    .in_6(n7432_4_out_12), .in_7(n7404_1_out_10), .in_8(n7404_1_out_7), .out_9(n7432_4_out_9),
    .out_10(n7432_4_out_10), .out_11(n7432_4_out_11), .out_12(n7432_4_out_12));
  _7432 u_7432_5 (
    .in_1(n7432_5_out_10), .in_2(n7432_5_out_12), .in_3(S2), .in_4(n7404_1_out_9), .in_5(n7432_6_out_9),
    .in_6(n7432_5_out_10), .in_7(n7404_1_out_10), .in_8(C1), .out_9(n7432_5_out_9), .out_10(n7432_5_out_10),
    .out_11(n7432_5_out_11), .out_12(n7432_5_out_12));
  _7432 u_7432_6 (
    .in_1(C2), .in_2(n7404_1_out_7), .in_3(n7432_6_out_12), .in_4(n7432_5_out_10), .in_7(n7404_1_out_10),
    .in_8(n7404_1_out_7), .out_9(n7432_6_out_9), .out_10(n7432_6_out_10), .out_12(n7432_6_out_12));  // open: in_5, in_6, out_11
  _7432 u_7432_7 (
    .in_1(n7432_7_out_10), .in_2(n7432_7_out_12), .in_3(n7404_1_out_8), .in_4(n7404_1_out_9),
    .in_7(n7404_1_out_10), .in_8(n7404_1_out_7), .out_9(n7432_7_out_9), .out_10(n7432_7_out_10),
    .out_12(n7432_7_out_12));  // open: in_5, in_6, out_11
  _7408 u_7408_1 (
    .in_1(n7432_2_out_9), .in_2(n7432_1_out_12), .in_3(n7432_1_out_11), .in_4(n7432_2_out_12),
    .in_5(n7408_1_out_12), .in_6(n7432_3_out_11), .in_7(n7408_1_out_9), .in_8(n7408_1_out_10),
    .out_9(n7408_1_out_9), .out_10(n7408_1_out_10), .out_11(n7408_1_out_11), .out_12(n7408_1_out_12));
  _7408 u_7408_2 (
    .in_1(n7408_2_out_10), .in_2(n7408_1_out_11), .in_3(n7432_4_out_9), .in_4(n7432_4_out_11),
    .in_5(n7408_3_out_9), .in_6(n7408_2_out_12), .in_7(n7432_5_out_9), .in_8(n7408_2_out_9),
    .out_9(n7408_2_out_9), .out_10(n7408_2_out_10), .out_11(out_5), .out_12(n7408_2_out_12));
  _7408 u_7408_3 (
    .in_1(n7408_3_out_10), .in_2(n7432_5_out_11), .in_3(n7432_6_out_10), .in_4(n7432_7_out_9),
    .out_9(n7408_3_out_9), .out_10(n7408_3_out_10));  // open: in_5, in_6, in_7, in_8, out_11, out_12

  // Notes on the sheet:
  //   S2'
  //   S1'
  //   C1'
  //   C2'
  //   S + S2' + C1 + C2'
  //   S + S2' + C1' + C2'
  //   S1 + S2 + C1 + C2
  //   S1 + S2 + C1 + C2'
  //   S1 + S2 + C1' + C2
  //   S1 + S2 + C1' + C2'
  //   S1 + S2' + C1' + C2
  //   S1' + S2 + C1 + C2'
  //   S1' + S2 + C1' + C2
  //   S1' + S2 + C1' + C2'
  //   S1' + S2' + C1' + C2'
endmodule

module _7408 (
  input  in_1,
  input  in_2,
  input  in_3,
  input  in_4,
  input  in_5,
  input  in_6,
  input  in_7,
  input  in_8,
  output out_9,
  output out_10,
  output out_11,
  output out_12
);

  and and_1 (out_9, in_1, in_2);
  and and_2 (out_10, in_3, in_4);
  and and_3 (out_11, in_5, in_6);
  and and_4 (out_12, in_7, in_8);
endmodule

module _7432 (
  input  in_1,
  input  in_2,
  input  in_3,
  input  in_4,
  input  in_5,
  input  in_6,
  input  in_7,
  input  in_8,
  output out_9,
  output out_10,
  output out_11,
  output out_12
);

  or or_1 (out_9, in_1, in_2);
  or or_2 (out_10, in_3, in_4);
  or or_3 (out_11, in_5, in_6);
  or or_4 (out_12, in_7, in_8);
endmodule

module _7404 (
  input  in_1,
  input  in_2,
  input  in_3,
  input  in_4,
  input  in_5,
  input  in_6,
  output out_7,
  output out_8,
  output out_9,
  output out_10,
  output out_11,
  output out_12
);

  not not_1 (out_7, in_1);
  not not_2 (out_8, in_2);
  not not_3 (out_9, in_3);
  not not_4 (out_10, in_4);
  not not_5 (out_11, in_5);
  not not_6 (out_12, in_6);
endmodule
