// Logisim project BCD Adder.circ as structural Verilog: 4 circuits, main circuit main
module main (
  input  in_1,
  input  in_2,
  input  in_3,
  input  in_4,
  input  in_5,
  input  in_6,
  input  in_7,
  input  in_8,
  input  in_9,
  output out_10,
  output out_11,
  output out_12,
  output out_13,
  output out_14
);

  wire n7408_1_out_11, n7408_1_out_12, n7432_1_out_12, n74283_1_c, n74283_1_out_10, n74283_1_out_11,
       n74283_1_out_12, n74283_1_s4__s3__s2__s1;

  _7432 u_7432_1 (
    .in_5(n74283_1_c), .in_6(n7432_1_out_12), .in_7(n7408_1_out_11), .in_8(n7408_1_out_12), .out_11(out_10),
    .out_12(n7432_1_out_12));  // open: in_1, in_2, in_3, in_4, out_9, out_10
  _7408 u_7408_1 (
    .in_5(n74283_1_out_12), .in_6(n74283_1_s4__s3__s2__s1), .in_7(n74283_1_out_12), .in_8(n74283_1_out_10),
    .out_11(n7408_1_out_11), .out_12(n7408_1_out_12));  // open: in_1, in_2, in_3, in_4, out_9, out_10
  _74283 u_74283_1 (
    .A4(in_1), .A3(in_2), .A2(in_3), .A1(in_4), .out_12(n74283_1_out_12), .C(n74283_1_c), .B4(in_5),
    .B3(in_6), .B2(in_7), .B1(in_8), .S4__S3__S2__S1(n74283_1_s4__s3__s2__s1), .out_10(n74283_1_out_10),
    .out_11(n74283_1_out_11));
  _74283 u_74283_2 (
    .A4(in_9), .A3(out_10), .A2(out_10), .A1(in_9), .out_12(out_11), .B4(n74283_1_out_12),
    .B3(n74283_1_s4__s3__s2__s1), .B2(n74283_1_out_10), .B1(n74283_1_out_11), .S4__S3__S2__S1(out_12),
    .out_10(out_13), .out_11(out_14));  // open: C
endmodule

module _74283 (
  input  A4,
  input  A3,
  input  A2,
  input  A1,
  input  B4,
  input  B3,
  input  B2,
  input  B1,
  output S4__S3__S2__S1,
  output out_10,
  output out_11,
  output out_12,
  output C
);

  wire adder_1_cout, adder_2_cout, adder_3_cout;

  Adder #(.width(1)) adder_1 (.a(A1), .b(B1), .out(out_11), .cout(adder_1_cout));  // open: cin
  Adder #(.width(1)) adder_2 (.a(A2), .b(B2), .out(out_10), .cin(adder_1_cout), .cout(adder_2_cout));
  Adder #(.width(1)) adder_3 (.a(A3), .b(B3), .out(S4__S3__S2__S1), .cin(adder_2_cout), .cout(adder_3_cout));
  Adder #(.width(1)) adder_4 (.a(A4), .b(B4), .out(out_12), .cin(adder_3_cout), .cout(C));
endmodule

module _7408 (
  input  in_1,
  input  in_2,
  input  in_3,
  input  in_4,
  input  in_5,
  input  in_6,
  input  in_7,
  input  in_8,
  output out_9,
  output out_10,
  output out_11,
  output out_12
);

  and and_1 (out_9, in_1, in_2);
  and and_2 (out_10, in_3, in_4);
  and and_3 (out_11, in_5, in_6);
  and and_4 (out_12, in_7, in_8);
endmodule

module _7432 (
  input  in_1,
  input  in_2,
  input  in_3,
  input  in_4,
  input  in_5,
  input  in_6,
  input  in_7,
  input  in_8,
  output out_9,
  output out_10,
  output out_11,
  output out_12
);

  or or_1 (out_9, in_1, in_2);
  or or_2 (out_10, in_3, in_4);
  or or_3 (out_11, in_5, in_6);
  or or_4 (out_12, in_7, in_8);
endmodule
