// Logisim project 231 Project using  D-flipflop.circ as structural Verilog: 1 circuit, main circuit main
module main (
  input  X____Y____Z,
  input  in_2,
  input  in_3
);

  wire and_1_out, and_2_out, and_3_out, clock_1_out, d_ff_1_q, d_ff_2_q, d_ff_3_q, d_ff_4_q, d_ff_5_q,
       d_ff_6_q, not_1_out, not_2_out, not_3_out, or_1_out, or_2_out, or_3_out, or_4_out, or_5_out, or_6_out;

  not not_1 (not_1_out, X____Y____Z);
  not not_2 (not_2_out, in_2);
  not not_3 (not_3_out, in_3);
  or or_1 (or_1_out, X____Y____Z, in_2, in_3);
  or or_2 (or_2_out, not_1_out, not_3_out);
  or or_3 (or_3_out, X____Y____Z, not_2_out);
  and and_1 (and_1_out, X____Y____Z, not_3_out);
  and and_2 (and_2_out, not_2_out, in_3);
  and and_3 (and_3_out, not_1_out, in_2);
  or or_4 (or_4_out, and_1_out, in_2);
  or or_5 (or_5_out, and_2_out, X____Y____Z);
  or or_6 (or_6_out, and_3_out, in_3);
  Clock clock_1 (.out(clock_1_out));
  D_Flip_Flop d_ff_1 (.clk(clock_1_out), .D(or_1_out), .Q(d_ff_1_q));  // open: Qn, preset, en, reset
  D_Flip_Flop d_ff_2 (.clk(clock_1_out), .D(or_2_out), .Q(d_ff_2_q));  // open: Qn, preset, en, reset
  D_Flip_Flop d_ff_3 (.clk(clock_1_out), .D(or_3_out), .Q(d_ff_3_q));  // open: Qn, preset, en, reset
  D_Flip_Flop d_ff_4 (.clk(clock_1_out), .D(or_4_out), .Q(d_ff_4_q));  // open: Qn, preset, en, reset
  D_Flip_Flop d_ff_5 (.clk(clock_1_out), .D(or_5_out), .Q(d_ff_5_q));  // open: Qn, preset, en, reset
  D_Flip_Flop d_ff_6 (.clk(clock_1_out), .D(or_6_out), .Q(d_ff_6_q));  // open: Qn, preset, en, reset
  _7_Segment_Display u_7_segment_display_1 (
    .g(d_ff_6_q), .f(d_ff_5_q), .a(d_ff_1_q), .b(d_ff_2_q), .e(d_ff_4_q), .d(d_ff_1_q), .c(d_ff_3_q));  // open: dp

  // Notes on the sheet:
  //   X'          Y'         Z'
  //   a = X + Y + z
  //   b = X' + Z'
  //   c = X+ Y'
  //   e = Y + XZ'
  //   f = X + Y'Z
  //   g = Z + X'Y
  //   d
endmodule
