// Logisim project Design the circuit using Decoder _ OR gates.circ as structural Verilog: 1 circuit, main circuit main
module main (
  input  X____Y____Z,
  input  in_2,
  input  in_3
);

  wire decoder_1_out0, decoder_1_out1, decoder_2_out0, decoder_2_out1, decoder_3_out0, decoder_3_out1,
       decoder_4_out1, decoder_5_out1, decoder_6_out1, or_1_out, or_2_out, or_3_out, or_4_out, or_5_out,
       or_6_out;

  Decoder decoder_1 (.out0(decoder_1_out0), .out1(decoder_1_out1), .sel(X____Y____Z));  // open: en
  Decoder decoder_2 (.out0(decoder_2_out0), .out1(decoder_2_out1), .sel(in_2));  // open: en
  Decoder decoder_3 (.out0(decoder_3_out0), .out1(decoder_3_out1), .sel(in_3));  // open: en
  Decoder decoder_4 (.out1(decoder_4_out1), .sel(X____Y____Z), .en(decoder_3_out0));  // open: out0
  Decoder decoder_5 (.out1(decoder_5_out1), .sel(in_3), .en(decoder_2_out0));  // open: out0
  Decoder decoder_6 (.out1(decoder_6_out1), .sel(in_2), .en(decoder_1_out0));  // open: out0
  or or_1 (or_1_out, decoder_1_out1, decoder_2_out1, decoder_3_out1);
  or or_2 (or_2_out, decoder_1_out0, decoder_3_out0);
  or or_3 (or_3_out, decoder_1_out1, decoder_2_out0);
  or or_4 (or_4_out, decoder_2_out1, decoder_4_out1);
  or or_5 (or_5_out, decoder_1_out1, decoder_5_out1);
  or or_6 (or_6_out, decoder_3_out1, decoder_6_out1);
  _7_Segment_Display u_7_segment_display_1 (
    .g(or_6_out), .f(or_5_out), .a(or_1_out), .b(or_2_out), .e(or_4_out), .d(or_1_out), .c(or_3_out));  // open: dp

  // Notes on the sheet:
  //   X'
  //   X
  //   Y'
  //   Y
  //   Z'
  //   Z
  //   x  x' y  y' z  z'
  //   a = X + Y + Z
  //   b = X' + Z'
  //   c = X + Y'
  //   e = Y+ XZ'
  //   f = X + Y'Z
  //   g = Z +X'Y
endmodule
