// Logisim project Design the circuit using NAND gates only.circ as structural Verilog: 1 circuit, main circuit main
module main (
  input  X,
  input  Y,
  input  Z
);

  wire nand_1_out, nand_2_out, nand_3_out, nand_4_out, nand_5_out, nand_6_out, nand_7_out, nand_8_out,
       nand_9_out, nand_10_out, nand_11_out, nand_12_out, nand_13_out, nand_14_out, nand_15_out, nand_16_out,
       nand_17_out, nand_18_out, nand_19_out, nand_20_out, nand_21_out, nand_22_out, nand_23_out,
       nand_24_out, nand_25_out;

  nand nand_1 (nand_1_out, X, X);
  nand nand_2 (nand_2_out, Y, Y);
  nand nand_3 (nand_3_out, Z, Z);
  nand nand_4 (nand_4_out, X, Z);
  nand nand_5 (nand_5_out, X, X);
  nand nand_6 (nand_6_out, Z, Z);
  nand nand_7 (nand_7_out, Y, Y);
  nand nand_8 (nand_8_out, Y, Y);
  nand nand_9 (nand_9_out, X, X);
  nand nand_10 (nand_10_out, nand_5_out, Y);
  nand nand_11 (nand_11_out, X, nand_6_out);
  nand nand_12 (nand_12_out, nand_8_out, Z);
  nand nand_13 (nand_13_out, nand_9_out, Y);
  nand nand_14 (nand_14_out, Z, Z);
  nand nand_15 (nand_15_out, nand_1_out, nand_2_out, nand_3_out);
  nand nand_16 (nand_16_out, nand_11_out, nand_11_out);
  nand nand_17 (nand_17_out, nand_12_out, nand_12_out);
  nand nand_18 (nand_18_out, X, X);
  nand nand_19 (nand_19_out, nand_13_out, nand_13_out);
  nand nand_20 (nand_20_out, nand_16_out, nand_16_out);
  nand nand_21 (nand_21_out, nand_17_out, nand_17_out);
  nand nand_22 (nand_22_out, nand_19_out, nand_19_out);
  nand nand_23 (nand_23_out, nand_20_out, nand_7_out);
  _7_Segment_Display u_7_segment_display_1 (
    .g(nand_25_out), .f(nand_24_out), .a(nand_15_out), .b(nand_4_out), .e(nand_23_out), .d(nand_15_out),
    .c(nand_10_out));  // open: dp
  nand nand_24 (nand_24_out, nand_21_out, nand_18_out);
  nand nand_25 (nand_25_out, nand_22_out, nand_14_out);

  // Notes on the sheet:
  //   b = X' + Z'
  //   c = X + Y'
  //   a = (x + y + z)
  //   d = (x + y + z)
  //   e = Y + XZ'
  //   f = X + Y'Z
  //   g = Z + X'Y
endmodule
