// Logisim project Generalized POS circuit with basic gates.circ as structural Verilog: 1 circuit, main circuit main
module main (
  input  X,
  input  Y,
  input  Z
);

  wire and_1_out, and_2_out, and_3_out, and_4_out, not_1_out, not_2_out, not_3_out, or_1_out, or_2_out,
       or_3_out, or_4_out, or_5_out, or_6_out, or_7_out, or_8_out, or_9_out, or_10_out, or_11_out, or_12_out,
       or_13_out;

  not not_1 (not_1_out, X);
  not not_2 (not_2_out, Y);
  not not_3 (not_3_out, Z);
  or or_1 (or_1_out, X, Y, Z);
  or or_2 (or_2_out, not_1_out, Y, not_3_out);
  or or_3 (or_3_out, X, not_2_out, Z);
  or or_4 (or_4_out, X, not_2_out, not_3_out);
  or or_5 (or_5_out, X, Y, Z);
  or or_6 (or_6_out, X, Y, not_3_out);
  or or_7 (or_7_out, not_1_out, Y, not_3_out);
  or or_8 (or_8_out, X, Y, Z);
  or or_9 (or_9_out, X, not_2_out, Z);
  or or_10 (or_10_out, X, not_2_out, not_3_out);
  or or_11 (or_11_out, X, Y, Z);
  or or_12 (or_12_out, not_1_out, Y, Z);
  or or_13 (or_13_out, not_1_out, not_2_out, Z);
  and and_1 (and_1_out, or_3_out, or_4_out);
  and and_2 (and_2_out, or_5_out, or_6_out, or_7_out);
  and and_3 (and_3_out, or_8_out, or_9_out, or_10_out);
  and and_4 (and_4_out, or_11_out, or_12_out, or_13_out);
  _7_Segment_Display u_7_segment_display_1 (
    .g(and_4_out), .f(and_3_out), .a(or_1_out), .b(or_2_out), .e(and_2_out), .d(or_1_out), .c(and_1_out));  // open: dp
endmodule
