// Logisim project 1st Canonical form.circ as structural Verilog: 1 circuit, main circuit main
module main (
  input  A,
  input  B,
  input  C,
  output F___A_prime_B_prime_C___BC_prime
);

  wire and_1_out, and_2_out, and_3_out, not_1_out, not_2_out, not_3_out;

  not not_1 (not_1_out, A);
  not not_2 (not_2_out, B);
  not not_3 (not_3_out, C);
  and and_1 (and_1_out, not_1_out, not_2_out);
  and and_2 (and_2_out, and_1_out, C);
  and and_3 (and_3_out, B, not_3_out);
  or or_1 (F___A_prime_B_prime_C___BC_prime, and_2_out, and_3_out);

  // Notes on the sheet:
  //   A'
  //   B'
  //   C'
  //   1st Canonical Form
  //   A'B'C
  //   BC'
endmodule
