// Logisim project b and c.circ as structural Verilog: 1 circuit, main circuit main
module main (
  input  A,
  input  B,
  input  C,
  input  D,
  input  A_2,
  input  B_2,
  input  C_2,
  input  D_2,
  output F___C_prime_D_prime___CD___B_prime,
  output F___C_prime___D___B
);

  wire and_1_out, and_2_out, not_1_out, not_2_out, not_3_out, not_4_out, or_1_out, or_2_out;

  not not_1 (not_1_out, C);
  not not_2 (not_2_out, D);
  not not_3 (not_3_out, B);
  and and_1 (and_1_out, not_1_out, not_2_out);
  and and_2 (and_2_out, C, D);
  not not_4 (not_4_out, C_2);
  or or_1 (or_1_out, not_4_out, D_2);
  or or_2 (or_2_out, and_1_out, and_2_out);
  or or_3 (F___C_prime___D___B, or_1_out, B_2);
  or or_4 (F___C_prime_D_prime___CD___B_prime, or_2_out, not_3_out);

  // Notes on the sheet:
  //   (B)
  //   (C)
endmodule
