// Logisim project 4 to 1 MUX.circ as structural Verilog: 1 circuit, main circuit main
module main (
  input  A,
  input  _0,
  input  _1,
  input  [1:0] B_C,
  output F
);

  wire not_1_out;

  not not_1 (not_1_out, A);
  Multiplexer #(.select(2)) multiplexer_1 (
    .in0(not_1_out), .in1(_1), .in2(_0), .in3(A), .out(F), .sel(B_C));  // open: en

  // Notes on the sheet:
  //   Figure: Logic Diagram for 4:1 MUX
endmodule
