// Logisim project 4 to 1 Multiplexer circuit.circ as structural Verilog: 1 circuit, main circuit main
module main (
  input  A0,
  input  A1,
  input  A2,
  input  A3,
  input  B,
  input  C,
  output out_7
);

  wire and_1_out, and_2_out, and_3_out, and_4_out, not_1_out, not_2_out, or_1_out, or_2_out;

  not not_1 (not_1_out, B);
  not not_2 (not_2_out, C);
  and and_1 (and_1_out, A0, not_1_out, not_2_out);
  and and_2 (and_2_out, A1, not_1_out, C);
  and and_3 (and_3_out, A2, B, not_2_out);
  and and_4 (and_4_out, A3, B, C);
  or or_1 (or_1_out, and_1_out, and_2_out);
  or or_2 (or_2_out, and_3_out, and_4_out);
  or or_3 (out_7, or_1_out, or_2_out);

  // Notes on the sheet:
  //   Figure: 4:1 Multiplexer
endmodule
