// Logisim project F3.circ as structural Verilog: 1 circuit, main circuit main
module main (
  input  A,
  input  B,
  input  C,
  input  A_2,
  input  B_2,
  input  C_2,
  output F___AC___BC_prime,
  output F___AC___BC_prime_2
);

  wire nand_1_out, nand_2_out, nand_3_out, nand_4_out, nand_5_out, nand_6_out, nand_7_out, nand_8_out,
       nand_10_out, nand_11_out;

  nand nand_1 (nand_1_out, C, C);
  nand nand_2 (nand_2_out, C_2, C_2);
  nand nand_3 (nand_3_out, A, C);
  nand nand_4 (nand_4_out, B, nand_1_out);
  nand nand_5 (nand_5_out, A_2, C_2);
  nand nand_6 (nand_6_out, B_2, nand_2_out);
  nand nand_7 (nand_7_out, nand_3_out, nand_3_out);
  nand nand_8 (nand_8_out, nand_4_out, nand_4_out);
  nand nand_9 (F___AC___BC_prime_2, nand_5_out, nand_6_out);
  nand nand_10 (nand_10_out, nand_7_out, nand_7_out);
  nand nand_11 (nand_11_out, nand_8_out, nand_8_out);
  nand nand_12 (F___AC___BC_prime, nand_10_out, nand_11_out);

  // Notes on the sheet:
  //   C'
  //   C'
  //   F: Experimental Data
  //   (AC)'
  //   (BC')'
  //   Part-01
  //   (AC)'
  //   (BC')'
  //   Part-02
  //   Figure F3: Universal (NAND) gate implementation of the circuit of Figure D2
  //   AC
  //   BC'
  //   (AC)'
  //   (BC')'
endmodule
