// Logisim project Universal NAND gate implemetation.circ as structural Verilog: 1 circuit, main circuit main
module main (
  input  A,
  input  B,
  input  C,
  input  A_2,
  input  B_2,
  input  C_2,
  output F___AC___BC_prime,
  output F___AC___BC_prime_2
);

  wire nand_1_out, nand_2_out, nand_3_out, nand_4_out, nand_5_out, nand_6_out, nand_7_out, nand_8_out,
       nand_9_out, nand_10_out;

  nand nand_1 (nand_1_out, C, C);
  nand nand_2 (nand_2_out, C_2, C_2);
  nand nand_3 (nand_3_out, A, C);
  nand nand_4 (nand_4_out, B, nand_1_out);
  nand nand_5 (nand_5_out, A_2, C_2);
  nand nand_6 (nand_6_out, B_2, nand_2_out);
  nand nand_7 (nand_7_out, nand_3_out, nand_3_out);
  nand nand_8 (nand_8_out, nand_4_out, nand_4_out);
  nand nand_9 (nand_9_out, nand_7_out, nand_7_out);
  nand nand_10 (nand_10_out, nand_8_out, nand_8_out);
  nand nand_11 (F___AC___BC_prime_2, nand_5_out, nand_6_out);
  nand nand_12 (F___AC___BC_prime, nand_9_out, nand_10_out);

  // Notes on the sheet:
  //   C'
  //   C'
  //   Step 1
  //   (AC)'
  //   (BC')'
  //   Step 2
  //   (BC')'
  //   Figure 0.2: Universal (NAND) gate implementation of the circuit of Figure 0.1
  //   AC
  //   BC'
  //   (AC)'
  //   (AC)'
  //   (BC')'
endmodule
