// Logisim project Minimal 1st canonical circuit of BCD to Excess-3 cnverter.circ as structural Verilog: 1 circuit, main circuit main
module main (
  input  W,
  input  X,
  input  Y,
  input  Z,
  output A___W___XZ___XY,
  output B___XY_prime_Z_prime___X_prime_Z___X_prime_Y,
  output C___Y_prime_Z_prime___YZ,
  output D___Z_prime
);

  wire and_1_out, and_2_out, and_3_out, and_4_out, and_5_out, and_6_out, and_7_out, and_8_out, not_1_out,
       not_2_out, not_3_out, not_4_out, not_5_out, not_6_out, or_1_out, or_2_out;

  not not_1 (not_1_out, Y);
  not not_2 (not_2_out, Z);
  not not_3 (not_3_out, X);
  not not_4 (not_4_out, X);
  not not_5 (not_5_out, Y);
  not not_6 (not_6_out, Z);
  and and_1 (and_1_out, X, Z);
  and and_2 (and_2_out, X, Y);
  and and_3 (and_3_out, X, not_1_out);
  and and_4 (and_4_out, not_3_out, Z);
  and and_5 (and_5_out, not_4_out, Y);
  and and_6 (and_6_out, not_5_out, not_6_out);
  and and_7 (and_7_out, Y, Z);
  or or_1 (or_1_out, W, and_1_out);
  and and_8 (and_8_out, and_3_out, not_2_out);
  or or_2 (or_2_out, and_8_out, and_4_out);
  or or_3 (A___W___XZ___XY, or_1_out, and_2_out);
  or or_4 (B___XY_prime_Z_prime___X_prime_Z___X_prime_Y, or_2_out, and_5_out);
  or or_5 (C___Y_prime_Z_prime___YZ, and_6_out, and_7_out);
  not not_7 (D___Z_prime, Z);

  // Notes on the sheet:
  //   Y'
  //   Z'
  //   X'
  //   X'
  //   Y'
  //   Z'
  //   XZ
  //   XY
  //   XY'
  //   X'Z
  //   X'Y
  //   Y'Z'
  //   YZ
  //   Figure F2: Minimal 1st canonical circuit of BCD to Excess-3 converter
  //   XY'Z'
  //   W + XZ
  //   XY'Z' + X'Z
endmodule
