// Logisim project Logic Circuit of a, b and c.circ as structural Verilog: 1 circuit, main circuit main
module main (
  input  A,
  input  B,
  input  C,
  input  D,
  input  A_2,
  input  B_2,
  input  C_2,
  input  D_2,
  input  A_3,
  input  B_3,
  input  C_3,
  input  D_3,
  output F1___A___C___BD___B_prime_D_prime,
  output F2___B_prime___CD___C_prime_D_prime,
  output F3___B___C_prime___D
);

  wire not_1_out, not_2_out, or_1_out, or_2_out, xnor_1_out, xnor_2_out;

  or or_1 (or_1_out, A, C);
  not not_1 (not_1_out, B_2);
  not not_2 (not_2_out, C_3);
  xnor xnor_1 (xnor_1_out, B, D);
  xnor xnor_2 (xnor_2_out, C_2, D_2);
  or or_2 (or_2_out, B_3, not_2_out);
  or or_3 (F1___A___C___BD___B_prime_D_prime, or_1_out, xnor_1_out);
  or or_4 (F2___B_prime___CD___C_prime_D_prime, not_1_out, xnor_2_out);
  or or_5 (F3___B___C_prime___D, or_2_out, D_3);

  // Notes on the sheet:
  //   C'
  //   A + C
  //   BD + B'D'
  //   Figure F1: Logic Circuit of a
  //   B'
  //   CD + C'D'
  //   Figure F2: Logic Circuit of b
  //   Figure F3: Logic Circuit of c
  //   B + C'
endmodule
