// Logisim project The Seven Segment Decoder Circuit.circ as structural Verilog: 1 circuit, main circuit main
module main (
  input  A,
  input  B,
  input  C,
  input  D,
  output out_5,
  output out_6,
  output out_7,
  output out_8,
  output out_9,
  output out_10,
  output out_11
);

  wire and_1_out, and_2_out, and_3_out, and_4_out, and_5_out, and_6_out, and_7_out, and_8_out, and_9_out,
       not_1_out, not_2_out, not_3_out, not_4_out, or_1_out, or_2_out, or_4_out, or_5_out, or_6_out,
       or_7_out, or_8_out, or_9_out, or_10_out, or_11_out;

  not not_1 (not_1_out, A);
  not not_2 (not_2_out, B);
  not not_3 (not_3_out, C);
  not not_4 (not_4_out, D);
  or or_1 (or_1_out, A, C);
  and and_1 (and_1_out, B, D);
  and and_2 (and_2_out, not_2_out, not_4_out);
  and and_3 (and_3_out, C, D);
  and and_4 (and_4_out, not_3_out, not_4_out);
  or or_2 (or_2_out, B, not_3_out);
  and and_5 (and_5_out, C, not_4_out);
  and and_6 (and_6_out, B, not_3_out);
  and and_7 (and_7_out, not_2_out, C);
  and and_8 (and_8_out, B, not_4_out);
  or or_3 (out_9, and_2_out, and_5_out);
  and and_9 (and_9_out, and_6_out, D);
  or or_4 (or_4_out, A, and_4_out);
  or or_5 (or_5_out, and_6_out, and_8_out);
  or or_6 (or_6_out, A, and_6_out);
  or or_7 (or_7_out, and_7_out, and_5_out);
  or or_8 (or_8_out, and_1_out, and_2_out);
  or or_9 (or_9_out, and_3_out, and_4_out);
  or or_10 (or_10_out, out_9, and_9_out);
  or or_11 (or_11_out, and_7_out, A);
  or or_12 (out_5, or_1_out, or_8_out);
  or or_13 (out_6, not_2_out, or_9_out);
  or or_14 (out_7, or_2_out, D);
  or or_15 (out_8, or_10_out, or_11_out);
  or or_16 (out_10, or_4_out, or_5_out);
  or or_17 (out_11, or_6_out, or_7_out);

  // Notes on the sheet:
  //   C'
  //   D'
  //   C'
  //   B'
  //   D'
  //   A +C
  //   BD
  //   B'D'
  //   B'
  //   CD
  //   C'D'
  //   B + C'
  //   CD'
  //   BC'
  //   B'C
  //   BD'
  //   Figure: The Seven Segment Decoder Circuit
  //   B'D' + CD'
  //   BC'D
  //   A + C'D'
  //   BC' + BD'
  //   A + BC'
  //   B'C + CD'
  //   CD + C'D'
  //   B'D' + CD' + BC'D
  //   BC' + A
  //   BD + B'D'
endmodule
