// Logisim project 8 to 1 Multiplexer.circ as structural Verilog: 1 circuit, main circuit main
module main (
  input  B0,
  input  B1,
  input  B2,
  input  B3,
  input  B4,
  input  B5,
  input  B6,
  input  B7,
  input  A,
  input  C,
  input  D,
  output F
);

  wire and_1_out, and_2_out, and_3_out, and_4_out, and_5_out, and_6_out, and_7_out, and_8_out, not_1_out,
       not_2_out, not_3_out, or_1_out, or_2_out, or_3_out, or_4_out, or_5_out, or_6_out;

  not not_1 (not_1_out, A);
  not not_2 (not_2_out, C);
  not not_3 (not_3_out, D);
  and and_1 (and_1_out, B0, not_1_out, not_2_out, not_3_out);
  and and_2 (and_2_out, B1, not_1_out, not_2_out, D);
  and and_3 (and_3_out, B2, not_1_out, C, not_3_out);
  and and_4 (and_4_out, B3, not_1_out, C, D);
  and and_5 (and_5_out, B4, A, not_2_out, not_3_out);
  and and_6 (and_6_out, B5, A, not_2_out, D);
  and and_7 (and_7_out, B6, A, C, not_3_out);
  and and_8 (and_8_out, B7, A, C, D);
  or or_1 (or_1_out, and_1_out, and_2_out);
  or or_2 (or_2_out, and_3_out, and_4_out);
  or or_3 (or_3_out, and_5_out, and_6_out);
  or or_4 (or_4_out, and_7_out, and_8_out);
  or or_5 (or_5_out, or_1_out, or_2_out);
  or or_6 (or_6_out, or_3_out, or_4_out);
  or or_7 (F, or_5_out, or_6_out);

  // Notes on the sheet:
  //   Figure: 8:1 Multiplexer
endmodule
