// Logisim project SR, JK, D _ T Flip Flops Diagrams.circ as structural Verilog: 1 circuit, main circuit main
module main (
  input  in_1,
  input  in_2,
  input  in_3,
  input  in_4,
  input  in_5,
  input  in_6,
  input  in_7,
  input  in_8,
  input  in_9,
  input  in_10,
  input  in_11,
  input  in_12,
  input  in_13,
  input  in_14,
  output out_15,
  output out_16,
  output out_17,
  output out_18,
  output out_19,
  output out_20,
  output out_21,
  output out_22
);

  wire clock_1_out, clock_2_out;

  Clock clock_1 (.out(clock_1_out));
  D_Flip_Flop d_ff_1 (
    .clk(clock_1_out), .D(in_10), .Q(out_20), .Qn(out_22), .en(in_13), .reset(in_14));  // open: preset
  S_R_Flip_Flop s_r_ff_1 (.S(in_1), .R(in_3), .Q(out_15), .Qn(out_17), .reset(in_6), .en(in_5));  // open: clk, preset
  Clock clock_2 (.out(clock_2_out));
  J_K_Flip_Flop j_k_ff_1 (.J(in_2), .K(in_4), .Q(out_16), .Qn(out_18), .en(in_7), .reset(in_8));  // open: clk, preset
  T_Flip_Flop t_ff_1 (.clk(clock_2_out), .T(in_9), .Q(out_19), .Qn(out_21), .reset(in_12), .en(in_11));  // open: preset

  // Notes on the sheet:
  //   Figure: Logic Diagram of S-R Flip Flop
  //   Figure: Logic Diagram of D Flip Flop
  //   Figure: Logic Diagram of J-K Flip Flop
  //   Figure: Logic Diagram of T Flip Flop
endmodule
