// Logisim project 4-bit adder using basic logic gates3.circ as structural Verilog: 1 circuit, main circuit main
module main (
  input  A0,
  input  A1,
  input  A2,
  input  A3,
  input  Carry_IN,
  input  B0,
  input  B1,
  input  B2,
  input  B3,
  output SUM0,
  output SUM1,
  output SUM2,
  output SUM3,
  output Carry_OUT
);

  wire adder_1_cout, adder_2_cout, adder_3_cout;

  Adder #(.width(1)) adder_1 (.a(A0), .b(B0), .out(SUM0), .cin(Carry_IN), .cout(adder_1_cout));
  Adder #(.width(1)) adder_2 (.a(A1), .b(B1), .out(SUM1), .cin(adder_1_cout), .cout(adder_2_cout));
  Adder #(.width(1)) adder_3 (.a(A2), .b(B2), .out(SUM2), .cin(adder_2_cout), .cout(adder_3_cout));
  Adder #(.width(1)) adder_4 (.a(A3), .b(B3), .out(SUM3), .cin(adder_3_cout), .cout(Carry_OUT));

  // Notes on the sheet:
  //   Figure E.1.2: 4-bit adder using basic logic gates
endmodule
