// Logisim project Logic Circuit of d and e.circ as structural Verilog: 1 circuit, main circuit main
module main (
  input  A,
  input  B,
  input  C,
  input  D,
  input  A_2,
  input  B_2,
  input  C_2,
  input  D_2,
  output F4___BC_prime_D___A___B_prime_C__B_prime_D_prime__CD_prime,
  output F5___B_prime_D_prime___CD_prime
);

  wire and_1_out, and_2_out, and_3_out, and_4_out, and_5_out, and_6_out, and_7_out, not_1_out, not_2_out,
       not_3_out, not_4_out, not_5_out, not_6_out, not_7_out, not_8_out, or_1_out, or_3_out, or_4_out;

  not not_1 (not_1_out, C);
  not not_2 (not_2_out, B);
  not not_3 (not_3_out, B);
  not not_4 (not_4_out, D);
  not not_5 (not_5_out, D);
  and and_1 (and_1_out, B, not_1_out);
  and and_2 (and_2_out, not_2_out, C);
  and and_3 (and_3_out, not_3_out, not_4_out);
  and and_4 (and_4_out, C, not_5_out);
  not not_6 (not_6_out, B_2);
  not not_7 (not_7_out, D_2);
  not not_8 (not_8_out, D_2);
  and and_5 (and_5_out, and_1_out, D);
  or or_1 (or_1_out, and_2_out, and_3_out);
  and and_6 (and_6_out, not_6_out, not_7_out);
  and and_7 (and_7_out, C_2, not_8_out);
  or or_2 (F5___B_prime_D_prime___CD_prime, and_6_out, and_7_out);
  or or_3 (or_3_out, and_5_out, A);
  or or_4 (or_4_out, or_1_out, and_4_out);
  or or_5 (F4___BC_prime_D___A___B_prime_C__B_prime_D_prime__CD_prime, or_3_out, or_4_out);

  // Notes on the sheet:
  //   C'
  //   B'
  //   B'
  //   D'
  //   D'
  //   BC'
  //   B'C
  //   B'D'
  //   CD'
  //   B'
  //   D'
  //   D'
  //   Figure F4: Logic Circuit of d
  //   B'D'
  //   CD'
  //   Figure F5: Logic Circuit of e
  //   BC'D
  //   B'C + B'D'
  //   BC'D + A
  //   B'C + B'D' + CD'
endmodule
