// Logisim project Logic Circuit of f and g.circ as structural Verilog: 1 circuit, main circuit main
module main (
  input  A,
  input  B,
  input  C,
  input  D,
  input  A_2,
  input  B_2,
  input  C_2,
  input  D_2,
  output F4___BC_prime_D___A___B_prime_C__B_prime_D_prime__CD_prime,
  output F7___A___BC_prime___B_prime_C___CD_prime
);

  wire and_1_out, and_2_out, and_3_out, and_4_out, not_1_out, not_2_out, not_3_out, not_4_out, not_5_out,
       or_1_out, or_2_out, or_3_out, xor_1_out;

  not not_1 (not_1_out, C);
  not not_2 (not_2_out, D);
  not not_3 (not_3_out, C);
  not not_4 (not_4_out, D);
  and and_1 (and_1_out, B, not_1_out);
  and and_2 (and_2_out, B, not_2_out);
  and and_3 (and_3_out, not_3_out, not_4_out);
  xor xor_1 (xor_1_out, B_2, C_2);
  not not_5 (not_5_out, D_2);
  or or_1 (or_1_out, A, and_1_out);
  or or_2 (or_2_out, and_2_out, and_3_out);
  or or_3 (or_3_out, A_2, xor_1_out);
  and and_4 (and_4_out, C_2, not_5_out);
  or or_4 (F4___BC_prime_D___A___B_prime_C__B_prime_D_prime__CD_prime, or_1_out, or_2_out);
  or or_5 (F7___A___BC_prime___B_prime_C___CD_prime, or_3_out, and_4_out);

  // Notes on the sheet:
  //   C'
  //   D'
  //   C'
  //   D'
  //   BC'
  //   BD'
  //   C'D'
  //   D'
  //   Figure F6: Logic Circuit of f
  //   BC' + B'C
  //   Figure F7: Logic Circuit of g
  //   A + BC'
  //   BD' + C'D'
  //   CD'
  //   A + BC' + B'C
endmodule
