// Logisim project 3 to 8 Decoder Circuit.circ as structural Verilog: 1 circuit, main circuit main
module main (
  input  A,
  input  C,
  input  D,
  output B0,
  output B1,
  output B2,
  output B3,
  output B4,
  output B5,
  output B6,
  output B7
);

  wire not_1_out, not_2_out, not_3_out;

  not not_1 (not_1_out, A);
  not not_2 (not_2_out, C);
  not not_3 (not_3_out, D);
  and and_1 (B0, not_1_out, not_2_out, not_3_out);
  and and_2 (B1, not_1_out, not_2_out, D);
  and and_3 (B2, not_1_out, C, not_3_out);
  and and_4 (B3, not_1_out, C, D);
  and and_5 (B4, A, not_2_out, not_3_out);
  and and_6 (B5, A, not_2_out, D);
  and and_7 (B6, A, C, not_3_out);
  and and_8 (B7, A, C, D);

  // Notes on the sheet:
  //   Figure: 3 to 8 Decoder Circuit
endmodule
