// Logisim project Logic Diagram for 8to1 MUX.circ as structural Verilog: 1 circuit, main circuit main
module main (
  input  B,
  input  _0,
  input  _1,
  input  [2:0] A_C_D,
  output F
);

  wire not_1_out;

  not not_1 (not_1_out, B);
  Multiplexer #(.select(3)) multiplexer_1 (
    .in0(_1), .in1(_1), .in2(_0), .in3(not_1_out), .in4(_0), .in5(not_1_out), .in6(B), .in7(B), .out(F),
    .sel(A_C_D));  // open: en

  // Notes on the sheet:
  //   Figure: Logic Diagram for 8:1 MUX
endmodule
