// Logisim project SR, JK, D _ T Flip Flops Circuits.circ as structural Verilog: 1 circuit, main circuit main
module main (
  input  R,
  input  K,
  input  J,
  input  S,
  input  D,
  input  T,
  output Q,
  output Q_2,
  output Q_prime,
  output Q_prime_2,
  output Q_3,
  output Q_4,
  output Q_prime_3,
  output Q_prime_4
);

  wire and_1_out, and_2_out, and_3_out, and_4_out, and_5_out, and_6_out, CLK_2_out, CLK_3_out, CLK_4_out,
       CLK_out, nand_1_out, nand_2_out, nand_3_out;

  Clock CLK (.out(CLK_out));
  Clock CLK_2 (.out(CLK_2_out));
  and and_1 (and_1_out, R, CLK_2_out);
  and and_2 (and_2_out, CLK_2_out, S);
  nand nand_1 (nand_1_out, D, D);
  nand nand_2 (nand_2_out, D, CLK_out);
  nand nand_3 (nand_3_out, CLK_out, nand_1_out);
  nor nor_1 (Q, and_1_out, Q_prime);
  nor nor_2 (Q_prime, Q, and_2_out);
  nand nand_4 (Q_4, nand_2_out, Q_prime_4);
  nand nand_5 (Q_prime_4, Q_4, nand_3_out);
  Clock CLK_3 (.out(CLK_3_out));
  Clock CLK_4 (.out(CLK_4_out));
  and and_3 (and_3_out, Q_2, K, CLK_3_out);
  and and_4 (and_4_out, CLK_3_out, J, Q_prime_2);
  and and_5 (and_5_out, Q_3, T, CLK_4_out);
  and and_6 (and_6_out, CLK_4_out, T, Q_prime_3);
  nor nor_3 (Q_2, and_3_out, Q_prime_2);
  nor nor_4 (Q_prime_2, Q_2, and_4_out);
  nor nor_5 (Q_3, and_5_out, Q_prime_3);
  nor nor_6 (Q_prime_3, Q_3, and_6_out);

  // Notes on the sheet:
  //   Figure: S-R Flip Flop Circuit
  //   Figure: D Flip Flop Circuit
  //   Figure: J-K Flip Flop Circuit
  //   Figure: T Flip Flop Circuit
endmodule
