// Logisim project ciam-project.circ as structural Verilog: 1 circuit, main circuit main
module main (
  input  A,
  input  Enable,
  input  in_3
);

  wire clock_1_out, j_k_ff_2_q, j_k_ff_3_q, multiplexer_1_out, multiplexer_2_out, multiplexer_3_out,
       multiplexer_4_out, multiplexer_5_out, multiplexer_6_out, multiplexer_7_out, multiplexer_8_out,
       not_1_out;
  wire [2:0] j_k_ff_3_qn;

  J_K_Flip_Flop j_k_ff_1 (
    .J(1'b1), .clk(j_k_ff_2_q), .K(1'b1), .Qn(j_k_ff_3_qn[2]), .reset(in_3));  // open: Q, preset, en
  J_K_Flip_Flop j_k_ff_2 (
    .J(1'b1), .clk(j_k_ff_3_q), .K(1'b1), .Q(j_k_ff_2_q), .Qn(j_k_ff_3_qn[1]), .reset(in_3));  // open: preset, en
  J_K_Flip_Flop j_k_ff_3 (
    .J(1'b1), .clk(clock_1_out), .K(1'b1), .Q(j_k_ff_3_q), .Qn(j_k_ff_3_qn[0]), .reset(in_3));  // open: preset, en
  Clock clock_1 (.out(clock_1_out));
  not not_1 (not_1_out, A);
  Multiplexer #(.select(3)) multiplexer_1 (
    .in0(1'b1), .in1(1'b1), .in2(1'b1), .in3(1'b0), .in4(1'b1), .in5(not_1_out), .in6(A), .in7(1'b0),
    .out(multiplexer_1_out), .sel(j_k_ff_3_qn), .en(Enable));
  Multiplexer #(.select(3)) multiplexer_2 (
    .in0(1'b0), .in1(1'b0), .in2(A), .in3(A), .in4(not_1_out), .in5(not_1_out), .in6(1'b1), .in7(1'b0),
    .out(multiplexer_2_out), .sel(j_k_ff_3_qn), .en(Enable));
  Multiplexer #(.select(3)) multiplexer_3 (
    .in0(1'b0), .in1(not_1_out), .in2(1'b0), .in3(A), .in4(A), .in5(not_1_out), .in6(1'b1), .in7(1'b0),
    .out(multiplexer_3_out), .sel(j_k_ff_3_qn), .en(Enable));
  Multiplexer #(.select(3)) multiplexer_4 (
    .in0(1'b1), .in1(1'b1), .in2(1'b1), .in3(1'b0), .in4(1'b1), .in5(not_1_out), .in6(A), .in7(1'b0),
    .out(multiplexer_4_out), .sel(j_k_ff_3_qn), .en(Enable));
  Multiplexer #(.select(3)) multiplexer_5 (
    .in0(1'b1), .in1(A), .in2(1'b1), .in3(1'b0), .in4(not_1_out), .in5(1'b0), .in6(1'b0), .in7(1'b0),
    .out(multiplexer_5_out), .sel(j_k_ff_3_qn), .en(Enable));
  Multiplexer #(.select(3)) multiplexer_6 (
    .in0(1'b1), .in1(1'b1), .in2(not_1_out), .in3(1'b0), .in4(A), .in5(1'b0), .in6(1'b0), .in7(1'b0),
    .out(multiplexer_6_out), .sel(j_k_ff_3_qn), .en(Enable));
  Multiplexer #(.select(3)) multiplexer_7 (
    .in0(1'b0), .in1(1'b1), .in2(1'b1), .in3(not_1_out), .in4(1'b1), .in5(1'b1), .in6(A), .in7(1'b0),
    .out(multiplexer_7_out), .sel(j_k_ff_3_qn));  // open: en
  Multiplexer #(.select(3)) multiplexer_8 (
    .in0(1'b0), .in1(1'b0), .in2(1'b0), .in3(1'b0), .in4(1'b0), .in5(1'b0), .in6(1'b0), .in7(1'b0),
    .out(multiplexer_8_out), .sel(j_k_ff_3_qn), .en(Enable));
  _7_Segment_Display u_7_segment_display_1 (
    .g(multiplexer_7_out), .f(multiplexer_6_out), .a(multiplexer_1_out), .b(multiplexer_2_out),
    .e(multiplexer_5_out), .d(multiplexer_4_out), .c(multiplexer_3_out), .dp(multiplexer_8_out));
endmodule
