// Logisim project Sec-8 G-08 D-Flip-Flop.circ as structural Verilog: 3 circuits, main circuit main
module main (
  input  Control,
  input  Clear
);

  wire CLK_out, d_ffs_1_p, d_ffs_1_q, d_ffs_1_r, d_ffs_1_s, universalgatecombi_1_a, universalgatecombi_1_b,
       universalgatecombi_1_c, universalgatecombi_1_d, universalgatecombi_1_dot, universalgatecombi_1_e,
       universalgatecombi_1_f, universalgatecombi_1_g;

  Clock CLK (.out(CLK_out));
  D_Flip_Flops d_ffs_1 (
    .CLK(CLK_out), .Control(Control), .CLR(Clear), .P(d_ffs_1_p), .Q(d_ffs_1_q), .R(d_ffs_1_r), .S(d_ffs_1_s));
  UniversalGateCombi universalgatecombi_1 (
    .P(d_ffs_1_p), .Q(d_ffs_1_q), .R(d_ffs_1_r), .S(d_ffs_1_s), .a(universalgatecombi_1_a),
    .f(universalgatecombi_1_f), .b(universalgatecombi_1_b), .g(universalgatecombi_1_g),
    .e(universalgatecombi_1_e), .c(universalgatecombi_1_c), .d(universalgatecombi_1_d),
    .dot(universalgatecombi_1_dot));
  _7_Segment_Display u_7_segment_display_1 (
    .g(universalgatecombi_1_g), .f(universalgatecombi_1_f), .a(universalgatecombi_1_a),
    .b(universalgatecombi_1_b), .e(universalgatecombi_1_e), .d(universalgatecombi_1_d),
    .c(universalgatecombi_1_c), .dp(universalgatecombi_1_dot));
endmodule

// D Flip-FLops
module D_Flip_Flops (
  input  CLK,
  input  Control,
  input  CLR,
  output P,
  output Q,
  output R,
  output S
);

  wire and_1_out, and_2_out, and_3_out, and_4_out, and_5_out, and_6_out, and_7_out, and_8_out, and_9_out,
       and_10_out, and_11_out, and_12_out, and_13_out, and_14_out, and_15_out, and_16_out, and_17_out,
       and_18_out, and_19_out, and_20_out, and_21_out, and_22_out, and_23_out, and_24_out, DP_out, DQ_out,
       DR_out, DS_out, not_1_out, P_qn, Q_qn, R_qn, S_qn;

  not not_1 (not_1_out, Control);
  D_Flip_Flop u_P (.clk(CLK), .D(DP_out), .Q(P), .Qn(P_qn), .reset(CLR));  // open: preset, en
  D_Flip_Flop u_Q (.clk(CLK), .D(DQ_out), .Q(Q), .Qn(Q_qn), .reset(CLR));  // open: preset, en
  D_Flip_Flop u_R (.clk(CLK), .D(DR_out), .Q(R), .Qn(R_qn), .reset(CLR));  // open: preset, en
  D_Flip_Flop u_S (.clk(CLK), .D(DS_out), .Q(S), .Qn(S_qn), .reset(CLR));  // open: preset, en
  and and_1 (and_1_out, Q, R, S);
  and and_2 (and_2_out, not_1_out, P, Q_qn);
  and and_3 (and_3_out, not_1_out, P, R_qn);
  and and_4 (and_4_out, P, Q_qn, R_qn);
  and and_5 (and_5_out, P, Q_qn, S_qn);
  and and_6 (and_6_out, Control, P_qn, Q);
  and and_7 (and_7_out, not_1_out, Q, R_qn);
  and and_8 (and_8_out, Control, Q_qn, R_qn);
  and and_9 (and_9_out, Control, Q_qn, S_qn);
  and and_10 (and_10_out, not_1_out, R_qn, S);
  and and_11 (and_11_out, P_qn, R, S_qn);
  and and_12 (and_12_out, Q_qn, R, S_qn);
  and and_13 (and_13_out, P, Q, S);
  and and_14 (and_14_out, Control, P_qn, R);
  and and_15 (and_15_out, Control, R, S_qn);
  and and_16 (and_16_out, not_1_out, P_qn, S_qn);
  and and_17 (and_17_out, not_1_out, Q_qn, S_qn);
  and and_18 (and_18_out, Control, P_qn, S);
  and and_19 (and_19_out, not_1_out, Q_qn, R, S);
  and and_20 (and_20_out, P_qn, Q_qn, R, S);
  and and_21 (and_21_out, not_1_out, P_qn, Q, S_qn);
  and and_22 (and_22_out, P, Q, R_qn, S_qn);
  and and_23 (and_23_out, Control, Q_qn, R_qn, S);
  and and_24 (and_24_out, Control, P, Q, S_qn);
  or DP (DP_out, and_1_out, and_2_out, and_3_out, and_4_out, and_5_out, and_6_out);
  or DQ (DQ_out, and_19_out, and_20_out, and_21_out, and_7_out, and_8_out, and_9_out);
  or DR (DR_out, and_10_out, and_11_out, and_12_out, and_13_out, and_14_out, and_15_out);
  or DS (DS_out, and_16_out, and_17_out, and_18_out, and_22_out, and_23_out, and_24_out);
endmodule

// NANDs
module UniversalGateCombi (
  input  P,
  input  Q,
  input  R,
  input  S,
  output a,
  output f,
  output b,
  output g,
  output e,
  output c,
  output d,
  output dot
);

  wire nand_1_out, nand_2_out, nand_3_out, nand_4_out, nand_5_out, nand_6_out, nand_7_out, nand_8_out,
       nand_9_out, nand_10_out, nand_11_out, nand_12_out, nand_13_out, nand_14_out, nand_15_out, nand_16_out,
       nand_17_out, nand_18_out, nand_19_out, nand_20_out, nand_21_out, nand_22_out, nand_23_out,
       nand_24_out, nand_25_out, nand_26_out, nand_27_out, nand_28_out, nand_29_out, nand_30_out,
       nand_31_out, nand_32_out, nand_33_out;

  nand nand_1 (nand_1_out, P, P);
  nand nand_2 (nand_2_out, Q, Q);
  nand nand_3 (nand_3_out, R, R);
  nand nand_4 (nand_4_out, S, S);
  nand nand_5 (nand_5_out, nand_1_out, nand_3_out, nand_4_out);
  nand nand_6 (nand_6_out, R, S);
  nand nand_7 (nand_7_out, P, R);
  nand nand_8 (nand_8_out, nand_2_out, nand_3_out);
  nand nand_9 (nand_9_out, nand_2_out, nand_4_out);
  nand nand_10 (nand_10_out, Q, R, S);
  nand nand_11 (nand_11_out, P, nand_2_out);
  nand nand_12 (nand_12_out, R, S);
  nand nand_13 (nand_13_out, nand_1_out, Q, nand_3_out);
  nand nand_14 (nand_14_out, P, nand_2_out, S);
  nand nand_15 (nand_15_out, P, R);
  nand nand_16 (nand_16_out, nand_1_out, nand_2_out, S);
  nand nand_17 (nand_17_out, nand_2_out, R);
  nand nand_18 (nand_18_out, R, S);
  nand nand_19 (nand_19_out, Q, nand_3_out, nand_4_out);
  nand nand_20 (nand_20_out, P, Q, nand_3_out);
  nand nand_21 (nand_21_out, nand_2_out, nand_4_out);
  nand nand_22 (nand_22_out, R, S);
  nand nand_23 (nand_23_out, nand_3_out, S);
  nand nand_24 (nand_24_out, Q, nand_3_out);
  nand nand_25 (nand_25_out, Q, S);
  nand nand_26 (nand_26_out, P, nand_4_out);
  nand nand_27 (nand_27_out, nand_1_out, nand_2_out);
  nand nand_28 (nand_28_out, nand_1_out, nand_3_out, nand_4_out);
  nand nand_29 (nand_29_out, nand_2_out, nand_3_out);
  nand nand_30 (nand_30_out, nand_1_out, R, S);
  nand nand_31 (nand_31_out, P, nand_3_out, S);
  nand nand_32 (nand_32_out, P, R, nand_4_out);
  nand nand_33 (nand_33_out, nand_1_out, Q, R, nand_4_out);
  nand nand_34 (e, nand_21_out, nand_22_out, nand_1_out);
  nand nand_35 (dot, nand_33_out, nand_33_out);
  nand nand_36 (a, nand_5_out, Q, nand_6_out, nand_7_out);
  nand nand_37 (f, nand_8_out, nand_9_out, nand_10_out, nand_11_out);
  nand nand_38 (b, nand_12_out, nand_13_out, nand_14_out, nand_15_out);
  nand nand_39 (g, nand_16_out, nand_17_out, nand_18_out, nand_19_out, nand_20_out);
  nand nand_40 (c, nand_23_out, nand_24_out, nand_25_out, nand_26_out);
  nand nand_41 (d, nand_27_out, nand_28_out, nand_29_out, nand_30_out, nand_31_out, nand_32_out);
endmodule
