// Logisim project Sec-8 G-08 Mux.circ as structural Verilog: 10 circuits, main circuit main
module main (
  input  [2:0] PQR,
  input  S
);

  wire mux_a_1_out_3, mux_b_1_out_3, mux_c_1_out_3, mux_d_1_out_3, mux_dot_1_out_3, mux_e_1_out_3,
       mux_f_1_out_3, mux_g_1_out_3;

  Mux_A mux_a_1 (.out_3(mux_a_1_out_3), .S(S), .in_2(PQR));
  Mux_f mux_f_1 (.out_3(mux_f_1_out_3), .S(S), .in_2(PQR));
  Mux_b mux_b_1 (.out_3(mux_b_1_out_3), .S(S), .in_2(PQR));
  Mux_g mux_g_1 (.out_3(mux_g_1_out_3), .S(S), .in_2(PQR));
  Mux_e mux_e_1 (.out_3(mux_e_1_out_3), .S(S), .in_2(PQR));
  Mux_c mux_c_1 (.out_3(mux_c_1_out_3), .S(S), .in_2(PQR));
  Mux_d mux_d_1 (.out_3(mux_d_1_out_3), .S(S), .in_2(PQR));
  Mux_dot mux_dot_1 (.out_3(mux_dot_1_out_3), .S(S), .in_2(PQR));
  _7_Segment_Display u_7_segment_display_1 (
    .g(mux_g_1_out_3), .f(mux_f_1_out_3), .a(mux_a_1_out_3), .b(mux_b_1_out_3), .e(mux_e_1_out_3),
    .d(mux_d_1_out_3), .c(mux_c_1_out_3), .dp(mux_dot_1_out_3));
endmodule

// a
module Mux_A (
  input  S,
  input  [2:0] in_2,
  output out_3
);

  wire not_1_out;

  not not_1 (not_1_out, S);
  Multiplexer #(.select(3)) multiplexer_1 (
    .in0(1'b1), .in1(1'b1), .in2(not_1_out), .in3(S), .in4(1'b1), .in5(1'b1), .in6(1'b0), .in7(1'b1),
    .out(out_3), .sel(in_2));  // open: en
endmodule

// f
module Mux_f (
  input  S,
  input  [2:0] in_2,
  output out_3
);

  wire not_1_out;

  not not_1 (not_1_out, S);
  Multiplexer #(.select(3)) multiplexer_1 (
    .in0(1'b1), .in1(not_1_out), .in2(1'b0), .in3(S), .in4(1'b1), .in5(1'b1), .in6(1'b0), .in7(1'b0),
    .out(out_3), .sel(in_2));  // open: en
endmodule

// b
module Mux_b (
  input  S,
  input  [2:0] in_2,
  output out_3
);

  wire not_1_out;

  not not_1 (not_1_out, S);
  Multiplexer #(.select(3)) multiplexer_1 (
    .in0(1'b0), .in1(S), .in2(1'b1), .in3(S), .in4(S), .in5(1'b1), .in6(1'b0), .in7(1'b1), .out(out_3),
    .sel(in_2));  // open: en
endmodule

module Template_mux (
  input  S,
  input  [2:0] in_2,
  output out_3
);

  wire not_1_out;

  not not_1 (not_1_out, S);
  Multiplexer #(.select(3)) multiplexer_1 (
    .out(out_3), .sel(in_2));  // open: in0, in1, in2, in3, in4, in5, in6, in7, en
endmodule

// g
module Mux_g (
  input  S,
  input  [2:0] in_2,
  output out_3
);

  wire not_1_out;

  not not_1 (not_1_out, S);
  Multiplexer #(.select(3)) multiplexer_1 (
    .in0(S), .in1(1'b1), .in2(not_1_out), .in3(S), .in4(1'b0), .in5(1'b1), .in6(1'b1), .in7(S), .out(out_3),
    .sel(in_2));  // open: en
endmodule

// e
module Mux_e (
  input  S,
  input  [2:0] in_2,
  output out_3
);

  wire not_1_out;

  not not_1 (not_1_out, S);
  Multiplexer #(.select(3)) multiplexer_1 (
    .in0(not_1_out), .in1(1'b1), .in2(1'b0), .in3(S), .in4(1'b1), .in5(1'b1), .in6(1'b1), .in7(1'b1),
    .out(out_3), .sel(in_2));  // open: en
endmodule

// c
module Mux_c (
  input  S,
  input  [2:0] in_2,
  output out_3
);

  wire not_1_out;

  not not_1 (not_1_out, S);
  Multiplexer #(.select(3)) multiplexer_1 (
    .in0(S), .in1(1'b0), .in2(1'b1), .in3(S), .in4(1'b1), .in5(not_1_out), .in6(1'b1), .in7(1'b1),
    .out(out_3), .sel(in_2));  // open: en
endmodule

// d
module Mux_d (
  input  S,
  input  [2:0] in_2,
  output out_3
);

  wire not_1_out;

  not not_1 (not_1_out, S);
  Multiplexer #(.select(3)) multiplexer_1 (
    .in0(1'b1), .in1(1'b1), .in2(not_1_out), .in3(S), .in4(1'b1), .in5(not_1_out), .in6(S), .in7(1'b1),
    .out(out_3), .sel(in_2));  // open: en
endmodule

// dot
module Mux_dot (
  input  S,
  input  [2:0] in_2,
  output out_3
);

  wire not_1_out;

  not not_1 (not_1_out, S);
  Multiplexer #(.select(3)) multiplexer_1 (
    .in0(1'b0), .in1(1'b0), .in2(1'b0), .in3(not_1_out), .in4(1'b0), .in5(1'b0), .in6(1'b0), .in7(1'b0),
    .out(out_3), .sel(in_2));  // open: en
endmodule
