// Logisim project Sec-8 G-08 UniversalGates.circ as structural Verilog: 2 circuits, main circuit main
module main (
  input  P,
  input  Q,
  input  R,
  input  S
);

  wire universalimp_1_a, universalimp_1_b, universalimp_1_c, universalimp_1_d, universalimp_1_dot,
       universalimp_1_e, universalimp_1_f, universalimp_1_g;

  UniversalImp universalimp_1 (
    .a(universalimp_1_a), .f(universalimp_1_f), .b(universalimp_1_b), .g(universalimp_1_g),
    .e(universalimp_1_e), .c(universalimp_1_c), .d(universalimp_1_d), .dot(universalimp_1_dot), .P(P), .Q(Q),
    .R(R), .S(S));
  _7_Segment_Display u_7_segment_display_1 (
    .g(universalimp_1_g), .f(universalimp_1_f), .a(universalimp_1_a), .b(universalimp_1_b),
    .e(universalimp_1_e), .d(universalimp_1_d), .c(universalimp_1_c), .dp(universalimp_1_dot));
endmodule

// NANDs
module UniversalImp (
  input  P,
  input  Q,
  input  R,
  input  S,
  output a,
  output f,
  output b,
  output g,
  output e,
  output c,
  output d,
  output dot
);

  wire nand_1_out, nand_2_out, nand_3_out, nand_4_out, nand_5_out, nand_6_out, nand_7_out, nand_8_out,
       nand_9_out, nand_10_out, nand_11_out, nand_12_out, nand_13_out, nand_14_out, nand_15_out, nand_16_out,
       nand_17_out, nand_18_out, nand_19_out, nand_20_out, nand_21_out, nand_22_out, nand_23_out,
       nand_24_out, nand_25_out, nand_26_out, nand_27_out, nand_28_out, nand_29_out, nand_30_out,
       nand_31_out, nand_32_out, nand_33_out;

  nand nand_1 (nand_1_out, P, P);
  nand nand_2 (nand_2_out, Q, Q);
  nand nand_3 (nand_3_out, R, R);
  nand nand_4 (nand_4_out, S, S);
  nand nand_5 (nand_5_out, nand_1_out, nand_3_out, nand_4_out);
  nand nand_6 (nand_6_out, R, S);
  nand nand_7 (nand_7_out, P, R);
  nand nand_8 (nand_8_out, nand_2_out, nand_3_out);
  nand nand_9 (nand_9_out, nand_2_out, nand_4_out);
  nand nand_10 (nand_10_out, Q, R, S);
  nand nand_11 (nand_11_out, P, nand_2_out);
  nand nand_12 (nand_12_out, R, S);
  nand nand_13 (nand_13_out, nand_1_out, Q, nand_3_out);
  nand nand_14 (nand_14_out, P, nand_2_out, S);
  nand nand_15 (nand_15_out, P, R);
  nand nand_16 (nand_16_out, nand_1_out, nand_2_out, S);
  nand nand_17 (nand_17_out, nand_2_out, R);
  nand nand_18 (nand_18_out, R, S);
  nand nand_19 (nand_19_out, Q, nand_3_out, nand_4_out);
  nand nand_20 (nand_20_out, P, Q, nand_3_out);
  nand nand_21 (nand_21_out, nand_2_out, nand_4_out);
  nand nand_22 (nand_22_out, R, S);
  nand nand_23 (nand_23_out, nand_3_out, S);
  nand nand_24 (nand_24_out, Q, nand_3_out);
  nand nand_25 (nand_25_out, Q, S);
  nand nand_26 (nand_26_out, P, nand_4_out);
  nand nand_27 (nand_27_out, nand_1_out, nand_2_out);
  nand nand_28 (nand_28_out, nand_1_out, nand_3_out, nand_4_out);
  nand nand_29 (nand_29_out, nand_2_out, nand_3_out);
  nand nand_30 (nand_30_out, nand_1_out, R, S);
  nand nand_31 (nand_31_out, P, nand_3_out, S);
  nand nand_32 (nand_32_out, P, R, nand_4_out);
  nand nand_33 (nand_33_out, nand_1_out, Q, R, nand_4_out);
  nand nand_34 (e, nand_21_out, nand_22_out, nand_1_out);
  nand nand_35 (dot, nand_33_out, nand_33_out);
  nand nand_36 (a, nand_5_out, Q, nand_6_out, nand_7_out);
  nand nand_37 (f, nand_8_out, nand_9_out, nand_10_out, nand_11_out);
  nand nand_38 (b, nand_12_out, nand_13_out, nand_14_out, nand_15_out);
  nand nand_39 (g, nand_16_out, nand_17_out, nand_18_out, nand_19_out, nand_20_out);
  nand nand_40 (c, nand_23_out, nand_24_out, nand_25_out, nand_26_out);
  nand nand_41 (d, nand_27_out, nand_28_out, nand_29_out, nand_30_out, nand_31_out, nand_32_out);
endmodule
