// Logisim project Sec-8-G-08-Decoder.circ as structural Verilog: 9 circuits, main circuit main
module main (
  input  [3:0] PQRS
);

  wire dec_a_1_out_2, dec_b_1_out_2, dec_c_1_out_2, dec_d_1_out_2, dec_dot_1_out_2, dec_e_1_out_2,
       dec_f_1_out_2, dec_g_1_out_2;

  Dec_a dec_a_1 (.PQRS(PQRS), .out_2(dec_a_1_out_2));
  Dec_f dec_f_1 (.PQRS(PQRS), .out_2(dec_f_1_out_2));
  Dec_b dec_b_1 (.PQRS(PQRS), .out_2(dec_b_1_out_2));
  Dec_g dec_g_1 (.PQRS(PQRS), .out_2(dec_g_1_out_2));
  Dec_e dec_e_1 (.PQRS(PQRS), .out_2(dec_e_1_out_2));
  Dec_c dec_c_1 (.PQRS(PQRS), .out_2(dec_c_1_out_2));
  Dec_d dec_d_1 (.PQRS(PQRS), .out_2(dec_d_1_out_2));
  Dec_dot dec_dot_1 (.PQRS(PQRS), .out_2(dec_dot_1_out_2));
  _7_Segment_Display u_7_segment_display_1 (
    .g(dec_g_1_out_2), .f(dec_f_1_out_2), .a(dec_a_1_out_2), .b(dec_b_1_out_2), .e(dec_e_1_out_2),
    .d(dec_d_1_out_2), .c(dec_c_1_out_2), .dp(dec_dot_1_out_2));
endmodule

// a
module Dec_a (
  input  [3:0] PQRS,
  output out_2
);

  wire decoder_1_out0, decoder_1_out1, decoder_1_out2, decoder_1_out3, decoder_1_out4, decoder_1_out7,
       decoder_1_out8, decoder_1_out9, decoder_1_out10, decoder_1_out11, decoder_1_out14;

  Decoder #(.select(4)) decoder_1 (
    .out0(decoder_1_out0), .out1(decoder_1_out1), .out2(decoder_1_out2), .out3(decoder_1_out3),
    .out4(decoder_1_out4), .out7(decoder_1_out7), .out8(decoder_1_out8), .out9(decoder_1_out9),
    .out10(decoder_1_out10), .out11(decoder_1_out11), .out14(decoder_1_out14), .sel(PQRS));  // open: out5, out6, out12, out13, out15, en
  or or_1 (out_2, decoder_1_out0, decoder_1_out1, decoder_1_out2, decoder_1_out3, decoder_1_out4, decoder_1_out7, decoder_1_out8, decoder_1_out9, decoder_1_out10, decoder_1_out11, decoder_1_out14);
endmodule

// f
module Dec_f (
  input  [3:0] PQRS,
  output out_2
);

  wire decoder_1_out0, decoder_1_out1, decoder_1_out2, decoder_1_out7, decoder_1_out8, decoder_1_out9,
       decoder_1_out10, decoder_1_out11;

  Decoder #(.select(4)) decoder_1 (
    .out0(decoder_1_out0), .out1(decoder_1_out1), .out2(decoder_1_out2), .out7(decoder_1_out7),
    .out8(decoder_1_out8), .out9(decoder_1_out9), .out10(decoder_1_out10), .out11(decoder_1_out11), .sel(PQRS));  // open: out3, out4, out5, out6, out12, out13, out14, out15, en
  or or_1 (out_2, decoder_1_out0, decoder_1_out1, decoder_1_out2, decoder_1_out7, decoder_1_out8, decoder_1_out9, decoder_1_out10, decoder_1_out11);
endmodule

// b
module Dec_b (
  input  [3:0] PQRS,
  output out_2
);

  wire decoder_1_out3, decoder_1_out4, decoder_1_out5, decoder_1_out7, decoder_1_out9, decoder_1_out10,
       decoder_1_out11, decoder_1_out14;

  Decoder #(.select(4)) decoder_1 (
    .out3(decoder_1_out3), .out4(decoder_1_out4), .out5(decoder_1_out5), .out7(decoder_1_out7),
    .out9(decoder_1_out9), .out10(decoder_1_out10), .out11(decoder_1_out11), .out14(decoder_1_out14),
    .sel(PQRS));  // open: out0, out1, out2, out6, out8, out12, out13, out15, en
  or or_1 (out_2, decoder_1_out3, decoder_1_out4, decoder_1_out5, decoder_1_out7, decoder_1_out9, decoder_1_out10, decoder_1_out11, decoder_1_out14);
endmodule

// g
module Dec_g (
  input  [3:0] PQRS,
  output out_2
);

  wire decoder_1_out1, decoder_1_out2, decoder_1_out3, decoder_1_out4, decoder_1_out7, decoder_1_out10,
       decoder_1_out11, decoder_1_out12, decoder_1_out13;

  Decoder #(.select(4)) decoder_1 (
    .out1(decoder_1_out1), .out2(decoder_1_out2), .out3(decoder_1_out3), .out4(decoder_1_out4),
    .out7(decoder_1_out7), .out10(decoder_1_out10), .out11(decoder_1_out11), .out12(decoder_1_out12),
    .out13(decoder_1_out13), .sel(PQRS));  // open: out0, out5, out6, out8, out9, out14, out15, en
  or or_1 (out_2, decoder_1_out1, decoder_1_out2, decoder_1_out3, decoder_1_out4, decoder_1_out7, decoder_1_out10, decoder_1_out11, decoder_1_out12, decoder_1_out13);
endmodule

// e
module Dec_e (
  input  [3:0] PQRS,
  output out_2
);

  wire decoder_1_out0, decoder_1_out2, decoder_1_out3, decoder_1_out7, decoder_1_out8, decoder_1_out9,
       decoder_1_out10, decoder_1_out11, decoder_1_out12, decoder_1_out13, decoder_1_out14;

  Decoder #(.select(4)) decoder_1 (
    .out0(decoder_1_out0), .out2(decoder_1_out2), .out3(decoder_1_out3), .out7(decoder_1_out7),
    .out8(decoder_1_out8), .out9(decoder_1_out9), .out10(decoder_1_out10), .out11(decoder_1_out11),
    .out12(decoder_1_out12), .out13(decoder_1_out13), .out14(decoder_1_out14), .sel(PQRS));  // open: out1, out4, out5, out6, out15, en
  or or_1 (out_2, decoder_1_out0, decoder_1_out2, decoder_1_out3, decoder_1_out7, decoder_1_out8, decoder_1_out9, decoder_1_out10, decoder_1_out11, decoder_1_out12, decoder_1_out13, decoder_1_out14);
endmodule

// c
module Dec_c (
  input  [3:0] PQRS,
  output out_2
);

  wire decoder_1_out1, decoder_1_out4, decoder_1_out5, decoder_1_out7, decoder_1_out8, decoder_1_out9,
       decoder_1_out10, decoder_1_out12, decoder_1_out13, decoder_1_out14;

  Decoder #(.select(4)) decoder_1 (
    .out1(decoder_1_out1), .out4(decoder_1_out4), .out5(decoder_1_out5), .out7(decoder_1_out7),
    .out8(decoder_1_out8), .out9(decoder_1_out9), .out10(decoder_1_out10), .out12(decoder_1_out12),
    .out13(decoder_1_out13), .out14(decoder_1_out14), .sel(PQRS));  // open: out0, out2, out3, out6, out11, out15, en
  or or_1 (out_2, decoder_1_out1, decoder_1_out4, decoder_1_out5, decoder_1_out7, decoder_1_out8, decoder_1_out9, decoder_1_out10, decoder_1_out12, decoder_1_out13, decoder_1_out14);
endmodule

// d
module Dec_d (
  input  [3:0] PQRS,
  output out_2
);

  wire decoder_1_out0, decoder_1_out1, decoder_1_out2, decoder_1_out3, decoder_1_out4, decoder_1_out7,
       decoder_1_out8, decoder_1_out9, decoder_1_out10, decoder_1_out13, decoder_1_out14;

  Decoder #(.select(4)) decoder_1 (
    .out0(decoder_1_out0), .out1(decoder_1_out1), .out2(decoder_1_out2), .out3(decoder_1_out3),
    .out4(decoder_1_out4), .out7(decoder_1_out7), .out8(decoder_1_out8), .out9(decoder_1_out9),
    .out10(decoder_1_out10), .out13(decoder_1_out13), .out14(decoder_1_out14), .sel(PQRS));  // open: out5, out6, out11, out12, out15, en
  or or_1 (out_2, decoder_1_out0, decoder_1_out1, decoder_1_out2, decoder_1_out3, decoder_1_out4, decoder_1_out7, decoder_1_out8, decoder_1_out9, decoder_1_out10, decoder_1_out13, decoder_1_out14);
endmodule

// dot
module Dec_dot (
  input  [3:0] PQRS,
  output out_2
);

  wire decoder_1_out6, decoder_1_out15;

  Decoder #(.select(4)) decoder_1 (
    .out6(decoder_1_out6), .out15(decoder_1_out15), .sel(PQRS));  // open: out0, out1, out2, out3, out4, out5, out7, out8, out9, out10, out11, out12, out13, out14, en
  or or_1 (out_2, decoder_1_out6, decoder_1_out15);
endmodule
