// Logisim project Universalgate.circ as structural Verilog: 1 circuit, main circuit main
module main (
  input  A_prime,
  input  B_prime,
  input  C_prime,
  input  D_prime,
  output a,
  output b,
  output c,
  output d,
  output e,
  output f,
  output g,
  output dot
);

  wire nand_1_out, nand_2_out, nand_3_out, nand_4_out, nand_5_out, nand_6_out, nand_7_out, nand_8_out,
       nand_9_out, nand_10_out, nand_11_out, nand_12_out, nand_13_out, nand_14_out, nand_15_out, nand_16_out,
       nand_17_out, nand_18_out, nand_19_out, nand_20_out, nand_21_out, nand_22_out, nand_23_out,
       nand_24_out, nand_25_out, nand_26_out, nand_27_out, nand_28_out, nand_29_out, nand_30_out, not_1_out,
       not_2_out, not_3_out, not_4_out;

  not not_1 (not_1_out, A_prime);
  not not_2 (not_2_out, B_prime);
  not not_3 (not_3_out, C_prime);
  not not_4 (not_4_out, D_prime);
  nand nand_1 (nand_1_out, not_2_out, not_2_out);
  nand nand_2 (nand_2_out, not_1_out, not_3_out);
  nand nand_3 (nand_3_out, not_4_out, not_3_out);
  nand nand_4 (nand_4_out, A_prime, C_prime, D_prime);
  nand nand_5 (nand_5_out, not_3_out, not_4_out);
  nand nand_6 (nand_6_out, not_1_out, B_prime, not_3_out);
  nand nand_7 (nand_7_out, not_1_out, B_prime, not_4_out);
  nand nand_8 (nand_8_out, A_prime, not_2_out, not_4_out);
  nand nand_9 (nand_9_out, C_prime, not_4_out);
  nand nand_10 (nand_10_out, B_prime, not_3_out, D_prime);
  nand nand_11 (nand_11_out, A_prime, not_2_out, not_3_out);
  nand nand_12 (nand_12_out, A_prime, B_prime, D_prime);
  nand nand_13 (nand_13_out, not_2_out, D_prime);
  nand nand_14 (nand_14_out, not_2_out, C_prime);
  nand nand_15 (nand_15_out, A_prime, C_prime);
  nand nand_16 (nand_16_out, not_1_out, not_3_out);
  nand nand_17 (nand_17_out, not_2_out, D_prime);
  nand nand_18 (nand_18_out, A_prime, D_prime);
  nand nand_19 (nand_19_out, A_prime, C_prime);
  nand nand_20 (nand_20_out, B_prime, not_3_out, not_4_out);
  nand nand_21 (nand_21_out, not_1_out, not_2_out);
  nand nand_22 (nand_22_out, not_2_out, not_3_out, D_prime);
  nand nand_23 (nand_23_out, not_2_out, C_prime, not_4_out);
  nand nand_24 (nand_24_out, A_prime, B_prime, not_3_out, not_4_out);
  nand nand_25 (nand_25_out, B_prime, not_3_out);
  nand nand_26 (nand_26_out, not_1_out, not_2_out, C_prime);
  nand nand_27 (nand_27_out, A_prime, not_2_out, D_prime);
  nand nand_28 (nand_28_out, A_prime, B_prime, not_4_out);
  nand nand_29 (nand_29_out, not_1_out, B_prime, C_prime, D_prime);
  nand nand_30 (nand_30_out, A_prime, C_prime, D_prime);
  nand nand_31 (dot, nand_29_out, nand_29_out);
  nand nand_32 (a, nand_1_out, nand_2_out, nand_3_out, nand_4_out);
  nand nand_33 (b, nand_5_out, nand_6_out, nand_30_out, nand_7_out, nand_8_out);
  nand nand_34 (c, nand_9_out, nand_10_out, nand_11_out, nand_12_out);
  nand nand_35 (d, nand_13_out, nand_14_out, nand_15_out, nand_16_out);
  nand nand_36 (e, nand_17_out, nand_18_out, nand_19_out, nand_20_out);
  nand nand_37 (f, nand_21_out, nand_22_out, nand_23_out, nand_24_out);
  nand nand_38 (g, nand_25_out, nand_26_out, nand_27_out, nand_28_out);
  _7_Segment_Display u_7_segment_display_1 (.g(g), .f(f), .a(a), .b(b), .e(e), .d(d), .c(c), .dp(dot));

  // Notes on the sheet:
  //   A
  //   B
  //   C
  //   D
  //   universal gate implementation
endmodule
